// Logisim project VPU.circ as structural Verilog: 32 circuits, main circuit main
module main (
  input  clk,
  input  rst,
  input  Jen,
  input  [31:0] Jin,
  output [31:0] R4_V,
  output [31:0] R5_V,
  output [31:0] R6_V,
  output [31:0] R7_V,
  output [31:0] R8_V,
  output [31:0] R9_V,
  output [31:0] R10_V,
  output [31:0] R11_V,
  output [31:0] R12_V,
  output [31:0] R13_V,
  output [31:0] R14_V,
  output [31:0] R15_V,
  output [31:0] R16_V,
  output [31:0] R17_V,
  output [31:0] R18_V,
  output [31:0] R19_V,
  output [31:0] R20_V,
  output [31:0] R21_V,
  output [31:0] R22_V,
  output [31:0] R23_V,
  output [31:0] R24_V,
  output [31:0] R25_V,
  output [31:0] R26_V,
  output [31:0] R27_V,
  output [31:0] R28_V,
  output [31:0] R29_V,
  output [31:0] R30_V,
  output [31:0] Jout,
  output [31:0] R31_V,
  output [31:0] R1,
  output [31:0] R2,
  output [31:0] R3,
  output [31:0] R4,
  output [31:0] R5,
  output [31:0] R6,
  output [31:0] R7,
  output InstDone,
  output [31:0] R8,
  output [31:0] R9,
  output [31:0] R10,
  output [31:0] R11,
  output [31:0] R12,
  output [31:0] R13,
  output [31:0] R14,
  output [31:0] R15,
  output [31:0] R16,
  output [31:0] R17,
  output [31:0] R18,
  output [31:0] R19,
  output [31:0] R20,
  output [31:0] R21,
  output [31:0] R22,
  output [31:0] R23,
  output [31:0] R24,
  output [31:0] R25,
  output [31:0] R26,
  output [31:0] R27,
  output [31:0] R28,
  output [31:0] R29,
  output [31:0] R30,
  output [31:0] R31
);

  wire ALUSrc, and_1_out, and_2_out, and_3_out, isBranch, isBranchN, isFROMCOP, isJump, isRType, isSLTI,
       isTOCOP, isVStore, MemtoReg, Neg, or_1_out, RegDest, RegDest_V, RegWrite, RegWrite_V, Zero;
  wire [1:0] cc_aluop, MemWrite;
  wire [2:0] multiplexer_12_out, multiplexer_14_out;
  wire [4:0] multiplexer_13_out, multiplexer_15_out;
  wire [5:0] ALU_Control_operation_number;
  wire [8:0] adder_2_out, multiplexer_1_out, multiplexer_2_out, multiplexer_7_out, PC, PCPlusOne;
  wire [31:0] aluV_aluout_0, aluV_aluout_1, aluV_aluout_2, aluV_aluout_3, D_MEM_jout, Dout0, Dout1, Dout2,
       Dout3, Dread1_128_0, Dread1_128_1, Dread1_128_2, Dread1_128_3, FromCOPOut, imm, J, multiplexer_3_out,
       multiplexer_4_out, multiplexer_5_out, multiplexer_6_out, multiplexer_8_out, multiplexer_9_out,
       multiplexer_10_out, multiplexer_11_out, multiplexer_16_out, multiplexer_17_out, multiplexer_19_out,
       multiplexer_20_out, multiplexer_21_out, regfileV_dread0_0, regfileV_dread0_1, regfileV_dread0_2,
       regfileV_dread0_3, RF_dread0, RF_dread1;

  Multiplexer #(.width(9)) multiplexer_1 (
    .in0(multiplexer_2_out), .in1({9{1'b0}}), .out(multiplexer_1_out), .sel(isJump));
  and and_1 (and_1_out, ~Zero, isBranchN);  // AND_Gate
  Multiplexer #(.width(9)) multiplexer_2 (
    .in0(multiplexer_7_out), .in1(adder_2_out), .out(multiplexer_2_out), .sel(or_1_out));
  or or_1 (or_1_out, and_1_out, and_2_out);
  Register #(.width(9)) register_1 (.D(multiplexer_1_out), .en(1'b1), .clk(clk), .Q(PC), .clr(rst));
  and and_2 (and_2_out, Zero, isBranch);
  jtag_ram512 I_MEM (.clk(clk), .Jen(Jen), .Jin(Jin), .Addr(PC), .Jout(J));  // open: Din, Wen, Dout
  Multiplexer #(.width(32)) multiplexer_3 (.in0(aluV_aluout_0), .in1(Dout0), .out(multiplexer_3_out), .sel(MemtoReg));
  Multiplexer #(.width(32)) multiplexer_4 (.in0(aluV_aluout_1), .in1(Dout1), .out(multiplexer_4_out), .sel(MemtoReg));
  Multiplexer #(.width(32)) multiplexer_5 (.in0(aluV_aluout_2), .in1(Dout2), .out(multiplexer_5_out), .sel(MemtoReg));
  Multiplexer #(.width(32)) multiplexer_6 (.in0(aluV_aluout_3), .in1(Dout3), .out(multiplexer_6_out), .sel(MemtoReg));
  Multiplexer #(.width(9)) multiplexer_7 (.in0(PC), .in1(PCPlusOne), .out(multiplexer_7_out), .sel(InstDone));
  Adder #(.width(9)) adder_1 (.a(9'h1), .b(PC), .out(PCPlusOne));  // open: cin, cout
  Multiplexer #(.width(32)) multiplexer_8 (
    .in0(multiplexer_3_out), .in1(RF_dread0), .out(multiplexer_8_out), .sel(isTOCOP));
  Multiplexer #(.width(32)) multiplexer_9 (
    .in0(multiplexer_4_out), .in1(RF_dread0), .out(multiplexer_9_out), .sel(isTOCOP));
  Multiplexer #(.width(32)) multiplexer_10 (
    .in0(multiplexer_5_out), .in1(RF_dread0), .out(multiplexer_10_out), .sel(isTOCOP));
  Multiplexer #(.width(32)) multiplexer_11 (
    .in0(multiplexer_6_out), .in1(RF_dread0), .out(multiplexer_11_out), .sel(isTOCOP));
  Adder #(.width(9)) adder_2 (.a(PCPlusOne), .b({9{1'b0}}), .out(adder_2_out));  // open: cin, cout
  assign imm = {{16{1'b0}}, {16{1'b0}}};  // Bit_Extender bit_extender_1
  Multiplexer #(.width(3)) multiplexer_12 (.in0(3'b100), .in1(3'b000), .out(multiplexer_12_out), .sel(RegDest_V));
  Multiplexer #(.width(5)) multiplexer_13 (.in0(5'b10000), .in1({5{1'b0}}), .out(multiplexer_13_out), .sel(RegDest));
  control_circuit cc (
    .opcode(6'b100100), .RegDest(RegDest), .ALUSrc(ALUSrc), .ALUOp(cc_aluop), .MemWrite(MemWrite),
    .MemToReg(MemtoReg), .RegWrite(RegWrite), .isBranchN(isBranchN), .isJump(isJump), .isSLTI(isSLTI),
    .isBranch(isBranch), .RegWrite_V(RegWrite_V), .RegDest_V(RegDest_V), .is_TOCOP(isTOCOP),
    .is_FROMCOP(isFROMCOP), .isVStore(isVStore), .isRType(isRType));
  Multiplexer #(.width(3)) multiplexer_14 (
    .in0(3'b000), .in1(multiplexer_12_out), .out(multiplexer_14_out), .sel(RegWrite_V));
  Multiplexer #(.width(5)) multiplexer_15 (
    .in0({5{1'b0}}), .in1(multiplexer_13_out), .out(multiplexer_15_out), .sel(RegWrite));
  Multiplexer #(.width(32)) multiplexer_16 (
    .in0(multiplexer_17_out), .in1(FromCOPOut), .out(multiplexer_16_out), .sel(isFROMCOP));
  Multiplexer #(.width(32)) multiplexer_17 (
    .in0(multiplexer_19_out), .in1(32'h1), .out(multiplexer_17_out), .sel(and_3_out));
  regfile_vector regfileV (
    .clk(clk), .rst(rst), .Dwrite0(multiplexer_8_out), .Dwrite1(multiplexer_9_out),
    .Dwrite2(multiplexer_10_out), .Dwrite3(multiplexer_11_out), .is_tocop(isTOCOP), .bit_tocop(2'b00),
    .Awrite(multiplexer_14_out), .Aread0(3'b000), .Aread1(3'b100), .Dread0_0(regfileV_dread0_0),
    .Dread0_1(regfileV_dread0_1), .Dread0_2(regfileV_dread0_2), .Dread0_3(regfileV_dread0_3),
    .Dread1_0(Dread1_128_0), .Dread1_1(Dread1_128_1), .Dread1_2(Dread1_128_2), .Dread1_3(Dread1_128_3),
    .R4(R4_V), .R5(R5_V), .R6(R6_V), .R7(R7_V), .R8(R8_V), .R9(R9_V), .R10(R10_V), .R11(R11_V), .R12(R12_V),
    .R13(R13_V), .R14(R14_V), .R15(R15_V), .R16(R16_V), .R17(R17_V), .R18(R18_V), .R19(R19_V), .R20(R20_V),
    .R21(R21_V), .R22(R22_V), .R23(R23_V), .R24(R24_V), .R25(R25_V), .R26(R26_V), .R27(R27_V), .R28(R28_V),
    .R29(R29_V), .R30(R30_V), .R31(R31_V));
  regfile RF (
    .clk(clk), .rst(rst), .Dwrite(multiplexer_16_out), .Awrite(multiplexer_15_out), .Aread0({5{1'b0}}),
    .Aread1(5'b10000), .Dread0(RF_dread0), .Dread1(RF_dread1), .R1(R1), .R2(R2), .R3(R3), .R4(R4), .R5(R5),
    .R6(R6), .R7(R7), .R8(R8), .R9(R9), .R10(R10), .R11(R11), .R12(R12), .R13(R13), .R14(R14), .R15(R15),
    .R16(R16), .R17(R17), .R18(R18), .R19(R19), .R20(R20), .R21(R21), .R22(R22), .R23(R23), .R24(R24),
    .R25(R25), .R26(R26), .R27(R27), .R28(R28), .R29(R29), .R30(R30), .R31(R31));
  and and_3 (and_3_out, isSLTI, Neg);
  Multiplexer #(.select(2), .width(32)) multiplexer_18 (
    .in0(regfileV_dread0_0), .in1(regfileV_dread0_1), .in2(regfileV_dread0_2), .in3(regfileV_dread0_3),
    .out(FromCOPOut), .sel(2'b00));
  Multiplexer #(.width(32)) multiplexer_19 (.in0(Jout), .in1(Dout0), .out(multiplexer_19_out), .sel(MemtoReg));
  Multiplexer #(.width(32)) multiplexer_20 (.in0(RF_dread1), .in1(imm), .out(multiplexer_20_out), .sel(ALUSrc));
  Multiplexer #(.width(32)) multiplexer_21 (
    .in0(RF_dread1), .in1(Dread1_128_0), .out(multiplexer_21_out), .sel(isVStore));
  jtag_ram512_128 D_MEM (
    .Din0(multiplexer_21_out), .Din1(Dread1_128_1), .Din2(Dread1_128_2), .Din3(Dread1_128_3), .clk(clk),
    .Jen(Jen), .Jin(J), .Wen(MemWrite), .Addr(Jout[10:2]), .Dout3(Dout3), .Dout2(Dout2), .Dout1(Dout1),
    .Dout0(Dout0), .Jout(D_MEM_jout));
  alu_circuit128 aluV (
    .aluop({6{1'b0}}), .a0(regfileV_dread0_0), .a1(regfileV_dread0_1), .a2(regfileV_dread0_2),
    .a3(regfileV_dread0_3), .b0(Dread1_128_0), .b1(Dread1_128_1), .b2(Dread1_128_2), .b3(Dread1_128_3),
    .aluOut_0(aluV_aluout_0), .aluOut_1(aluV_aluout_1), .aluOut_2(aluV_aluout_2), .aluOut_3(aluV_aluout_3));
  alu_circuit alu (
    .aluop(ALU_Control_operation_number), .a(RF_dread0), .b(multiplexer_20_out), .Shamt({5{1'b0}}),
    .clk(clk), .rst(rst), .aluOut(Jout), .ZeroFlag(Zero), .NegativeFlag(Neg), .Done(InstDone));
  alu_ctrl_circuit ALU_Control (.funct({6{1'b0}}), .ALUop(cc_aluop), .Operation_number(ALU_Control_operation_number));

  // Other names for the same wires on the sheet: AluOut[31:0] = Jout; Clock = clk; Done = InstDone; Reset = rst
endmodule

module jtag_ram8 (
  input  clk,
  input  Jen,
  input  [31:0] Din,
  input  [31:0] Jin,
  input  Wen,
  input  [2:0] Addr,
  output [31:0] Dout,
  output [31:0] Jout
);

  wire decoder_1_out0, decoder_1_out1, decoder_1_out2, decoder_1_out3, decoder_1_out4, decoder_1_out5,
       decoder_1_out6, decoder_1_out7, or_1_out, or_2_out, or_3_out, or_4_out, or_5_out, or_6_out, or_7_out,
       or_8_out;
  wire [31:0] M0, M1, M2, M3, M4, M5, M6, multiplexer_1_out, multiplexer_2_out, multiplexer_3_out,
       multiplexer_4_out, multiplexer_5_out, multiplexer_6_out, multiplexer_7_out, multiplexer_8_out;

  Decoder #(.select(3)) decoder_1 (
    .out0(decoder_1_out0), .out1(decoder_1_out1), .out2(decoder_1_out2), .out3(decoder_1_out3),
    .out4(decoder_1_out4), .out5(decoder_1_out5), .out6(decoder_1_out6), .out7(decoder_1_out7), .sel(Addr),
    .en(Wen));
  Multiplexer #(.width(32)) multiplexer_1 (.in0(Din), .in1(Jin), .out(multiplexer_1_out), .sel(Jen));
  Multiplexer #(.width(32)) multiplexer_2 (.in0(Din), .in1(M0), .out(multiplexer_2_out), .sel(Jen));
  Multiplexer #(.width(32)) multiplexer_3 (.in0(Din), .in1(M1), .out(multiplexer_3_out), .sel(Jen));
  Multiplexer #(.width(32)) multiplexer_4 (.in0(Din), .in1(M2), .out(multiplexer_4_out), .sel(Jen));
  Multiplexer #(.width(32)) multiplexer_5 (.in0(Din), .in1(M3), .out(multiplexer_5_out), .sel(Jen));
  Multiplexer #(.width(32)) multiplexer_6 (.in0(Din), .in1(M4), .out(multiplexer_6_out), .sel(Jen));
  Multiplexer #(.width(32)) multiplexer_7 (.in0(Din), .in1(M5), .out(multiplexer_7_out), .sel(Jen));
  Multiplexer #(.width(32)) multiplexer_8 (.in0(Din), .in1(M6), .out(multiplexer_8_out), .sel(Jen));
  Register #(.width(32)) register_1 (.D(multiplexer_1_out), .en(or_1_out), .clk(clk), .Q(M0));  // open: clr
  or or_1 (or_1_out, Jen, decoder_1_out0);
  Register #(.width(32)) register_2 (.D(multiplexer_2_out), .en(or_2_out), .clk(clk), .Q(M1));  // open: clr
  or or_2 (or_2_out, Jen, decoder_1_out1);
  Register #(.width(32)) register_3 (.D(multiplexer_3_out), .en(or_3_out), .clk(clk), .Q(M2));  // open: clr
  or or_3 (or_3_out, Jen, decoder_1_out2);
  Register #(.width(32)) register_4 (.D(multiplexer_4_out), .en(or_4_out), .clk(clk), .Q(M3));  // open: clr
  or or_4 (or_4_out, Jen, decoder_1_out3);
  Register #(.width(32)) register_5 (.D(multiplexer_5_out), .en(or_5_out), .clk(clk), .Q(M4));  // open: clr
  or or_5 (or_5_out, Jen, decoder_1_out4);
  Register #(.width(32)) register_6 (.D(multiplexer_6_out), .en(or_6_out), .clk(clk), .Q(M5));  // open: clr
  or or_6 (or_6_out, Jen, decoder_1_out5);
  Register #(.width(32)) register_7 (.D(multiplexer_7_out), .en(or_7_out), .clk(clk), .Q(M6));  // open: clr
  or or_7 (or_7_out, Jen, decoder_1_out6);
  Register #(.width(32)) register_8 (.D(multiplexer_8_out), .en(or_8_out), .clk(clk), .Q(Jout));  // open: clr
  or or_8 (or_8_out, Jen, decoder_1_out7);
  Multiplexer #(.select(3), .width(32)) multiplexer_9 (
    .in0(M0), .in1(M1), .in2(M2), .in3(M3), .in4(M4), .in5(M5), .in6(M6), .in7(Jout), .out(Dout), .sel(Addr));

  // Other names for the same wires on the sheet: M7[31:0] = Jout
endmodule

module jtag_ram64 (
  input  clk,
  input  Jen,
  input  [31:0] Din,
  input  [31:0] Jin,
  input  Wen,
  input  [5:0] Addr,
  output [31:0] Dout,
  output [31:0] Jout
);

  wire decoder_1_out0, decoder_1_out1, decoder_1_out2, decoder_1_out3, decoder_1_out4, decoder_1_out5,
       decoder_1_out6, decoder_1_out7;
  wire [31:0] b0_dout, b0_jout, b1_dout, b1_jout, b2_dout, b2_jout, b3_dout, b3_jout, b4_dout, b4_jout,
       b5_dout, b5_jout, b6_dout, b6_jout, b7_dout;

  Decoder #(.select(3)) decoder_1 (
    .out0(decoder_1_out0), .out1(decoder_1_out1), .out2(decoder_1_out2), .out3(decoder_1_out3),
    .out4(decoder_1_out4), .out5(decoder_1_out5), .out6(decoder_1_out6), .out7(decoder_1_out7),
    .sel(Addr[5:3]), .en(Wen));
  jtag_ram8 b0 (
    .clk(clk), .Jen(Jen), .Din(Din), .Jin(Jin), .Wen(decoder_1_out0), .Addr(Addr[2:0]), .Dout(b0_dout),
    .Jout(b0_jout));
  jtag_ram8 b1 (
    .clk(clk), .Jen(Jen), .Din(Din), .Jin(b0_jout), .Wen(decoder_1_out1), .Addr(Addr[2:0]), .Dout(b1_dout),
    .Jout(b1_jout));
  jtag_ram8 b2 (
    .clk(clk), .Jen(Jen), .Din(Din), .Jin(b1_jout), .Wen(decoder_1_out2), .Addr(Addr[2:0]), .Dout(b2_dout),
    .Jout(b2_jout));
  jtag_ram8 b3 (
    .clk(clk), .Jen(Jen), .Din(Din), .Jin(b2_jout), .Wen(decoder_1_out3), .Addr(Addr[2:0]), .Dout(b3_dout),
    .Jout(b3_jout));
  jtag_ram8 b4 (
    .clk(clk), .Jen(Jen), .Din(Din), .Jin(b3_jout), .Wen(decoder_1_out4), .Addr(Addr[2:0]), .Dout(b4_dout),
    .Jout(b4_jout));
  jtag_ram8 b5 (
    .clk(clk), .Jen(Jen), .Din(Din), .Jin(b4_jout), .Wen(decoder_1_out5), .Addr(Addr[2:0]), .Dout(b5_dout),
    .Jout(b5_jout));
  jtag_ram8 b6 (
    .clk(clk), .Jen(Jen), .Din(Din), .Jin(b5_jout), .Wen(decoder_1_out6), .Addr(Addr[2:0]), .Dout(b6_dout),
    .Jout(b6_jout));
  jtag_ram8 b7 (
    .clk(clk), .Jen(Jen), .Din(Din), .Jin(b6_jout), .Wen(decoder_1_out7), .Addr(Addr[2:0]), .Dout(b7_dout),
    .Jout(Jout));
  Multiplexer #(.select(3), .width(32)) multiplexer_1 (
    .in0(b0_dout), .in1(b1_dout), .in2(b2_dout), .in3(b3_dout), .in4(b4_dout), .in5(b5_dout), .in6(b6_dout),
    .in7(b7_dout), .out(Dout), .sel(Addr[5:3]));
endmodule

module jtag_ram512 (
  input  clk,
  input  Jen,
  input  [31:0] Din,
  input  [31:0] Jin,
  input  Wen,
  input  [8:0] Addr,
  output [31:0] Jout,
  output [31:0] Dout
);

  wire decoder_1_out0, decoder_1_out1, decoder_1_out2, decoder_1_out3, decoder_1_out4, decoder_1_out5,
       decoder_1_out6, decoder_1_out7;
  wire [31:0] b0_dout, b0_jout, b1_dout, b1_jout, b2_dout, b2_jout, b3_dout, b3_jout, b4_dout, b4_jout,
       b5_dout, b5_jout, b6_dout, b6_jout, b7_dout;

  Decoder #(.select(3)) decoder_1 (
    .out0(decoder_1_out0), .out1(decoder_1_out1), .out2(decoder_1_out2), .out3(decoder_1_out3),
    .out4(decoder_1_out4), .out5(decoder_1_out5), .out6(decoder_1_out6), .out7(decoder_1_out7),
    .sel(Addr[8:6]), .en(Wen));
  jtag_ram64 b0 (
    .clk(clk), .Jen(Jen), .Din(Din), .Jin(Jin), .Wen(decoder_1_out0), .Addr(Addr[5:0]), .Dout(b0_dout),
    .Jout(b0_jout));
  jtag_ram64 b1 (
    .clk(clk), .Jen(Jen), .Din(Din), .Jin(b0_jout), .Wen(decoder_1_out1), .Addr(Addr[5:0]), .Dout(b1_dout),
    .Jout(b1_jout));
  jtag_ram64 b2 (
    .clk(clk), .Jen(Jen), .Din(Din), .Jin(b1_jout), .Wen(decoder_1_out2), .Addr(Addr[5:0]), .Dout(b2_dout),
    .Jout(b2_jout));
  jtag_ram64 b3 (
    .clk(clk), .Jen(Jen), .Din(Din), .Jin(b2_jout), .Wen(decoder_1_out3), .Addr(Addr[5:0]), .Dout(b3_dout),
    .Jout(b3_jout));
  jtag_ram64 b4 (
    .clk(clk), .Jen(Jen), .Din(Din), .Jin(b3_jout), .Wen(decoder_1_out4), .Addr(Addr[5:0]), .Dout(b4_dout),
    .Jout(b4_jout));
  jtag_ram64 b5 (
    .clk(clk), .Jen(Jen), .Din(Din), .Jin(b4_jout), .Wen(decoder_1_out5), .Addr(Addr[5:0]), .Dout(b5_dout),
    .Jout(b5_jout));
  jtag_ram64 b6 (
    .clk(clk), .Jen(Jen), .Din(Din), .Jin(b5_jout), .Wen(decoder_1_out6), .Addr(Addr[5:0]), .Dout(b6_dout),
    .Jout(b6_jout));
  jtag_ram64 b7 (
    .clk(clk), .Jen(Jen), .Din(Din), .Jin(b6_jout), .Wen(decoder_1_out7), .Addr(Addr[5:0]), .Dout(b7_dout),
    .Jout(Jout));
  Multiplexer #(.select(3), .width(32)) multiplexer_1 (
    .in0(b0_dout), .in1(b1_dout), .in2(b2_dout), .in3(b3_dout), .in4(b4_dout), .in5(b5_dout), .in6(b6_dout),
    .in7(b7_dout), .out(Dout), .sel(Addr[8:6]));
endmodule

module regfile (
  input  clk,
  input  rst,
  input  [31:0] Dwrite,
  input  [4:0] Awrite,
  input  [4:0] Aread0,
  input  [4:0] Aread1,
  output [31:0] Dread0,
  output [31:0] Dread1,
  output [31:0] R1,
  output [31:0] R2,
  output [31:0] R3,
  output [31:0] R4,
  output [31:0] R5,
  output [31:0] R6,
  output [31:0] R7,
  output [31:0] R8,
  output [31:0] R9,
  output [31:0] R10,
  output [31:0] R11,
  output [31:0] R12,
  output [31:0] R13,
  output [31:0] R14,
  output [31:0] R15,
  output [31:0] R16,
  output [31:0] R17,
  output [31:0] R18,
  output [31:0] R19,
  output [31:0] R20,
  output [31:0] R21,
  output [31:0] R22,
  output [31:0] R23,
  output [31:0] R24,
  output [31:0] R25,
  output [31:0] R26,
  output [31:0] R27,
  output [31:0] R28,
  output [31:0] R29,
  output [31:0] R30,
  output [31:0] R31
);

  wire and_1_out, and_2_out, and_3_out, and_4_out, and_5_out, and_6_out, and_7_out, and_8_out, and_9_out,
       and_10_out, and_11_out, and_12_out, and_13_out, and_14_out, and_15_out, and_16_out, and_17_out,
       and_18_out, and_19_out, and_20_out, and_21_out, and_22_out, and_23_out, and_24_out, and_25_out,
       and_26_out, and_27_out, and_28_out, and_29_out, and_30_out, and_31_out, and_32_out, decoder_1_out0,
       decoder_1_out1, decoder_1_out2, decoder_1_out3, decoder_1_out4, decoder_1_out5, decoder_1_out6,
       decoder_1_out7, decoder_2_out0, decoder_2_out1, decoder_2_out2, decoder_2_out3, or_1_out, or_2_out,
       or_3_out, or_4_out, or_5_out, or_6_out, or_7_out, or_8_out, or_9_out, or_10_out, or_11_out, or_12_out,
       or_13_out, or_14_out, or_15_out, or_16_out, or_17_out, or_18_out, or_19_out, or_20_out, or_21_out,
       or_22_out, or_23_out, or_24_out, or_25_out, or_26_out, or_27_out, or_28_out, or_29_out, or_30_out,
       or_31_out, or_32_out, undriven_2, undriven_3, undriven_4, undriven_5;
  wire [31:0] multiplexer_1_out, multiplexer_2_out, multiplexer_3_out, multiplexer_4_out, multiplexer_5_out,
       multiplexer_6_out, multiplexer_7_out, multiplexer_8_out, multiplexer_9_out, undriven;

  Register #(.width(32)) register_1 (.D(undriven), .en(or_1_out), .clk(undriven_2));  // open: Q, clr
  or or_1 (or_1_out, undriven_5, and_1_out);
  and and_1 (and_1_out, undriven_4, undriven_3);
  Decoder #(.select(3)) decoder_1 (
    .out0(decoder_1_out0), .out1(decoder_1_out1), .out2(decoder_1_out2), .out3(decoder_1_out3),
    .out4(decoder_1_out4), .out5(decoder_1_out5), .out6(decoder_1_out6), .out7(decoder_1_out7),
    .sel(Awrite[4:2]));  // open: en
  Decoder #(.select(2)) decoder_2 (
    .out0(decoder_2_out0), .out1(decoder_2_out1), .out2(decoder_2_out2), .out3(decoder_2_out3),
    .sel(Awrite[1:0]));  // open: en
  Multiplexer #(.width(32)) multiplexer_1 (.in0(Dwrite), .in1({32{1'b0}}), .out(multiplexer_1_out), .sel(rst));
  and and_2 (and_2_out, decoder_2_out0, decoder_1_out1);
  and and_3 (and_3_out, decoder_2_out0, decoder_1_out2);
  and and_4 (and_4_out, decoder_2_out0, decoder_1_out3);
  and and_5 (and_5_out, decoder_2_out0, decoder_1_out4);
  and and_6 (and_6_out, decoder_2_out0, decoder_1_out5);
  and and_7 (and_7_out, decoder_2_out0, decoder_1_out6);
  and and_8 (and_8_out, decoder_2_out0, decoder_1_out7);
  Register #(.width(32)) register_2 (.D(multiplexer_1_out), .en(or_2_out), .clk(clk), .Q(R4));  // open: clr
  or or_2 (or_2_out, rst, and_2_out);
  Register #(.width(32)) register_3 (.D(multiplexer_1_out), .en(or_3_out), .clk(clk), .Q(R8));  // open: clr
  or or_3 (or_3_out, rst, and_3_out);
  Register #(.width(32)) register_4 (.D(multiplexer_1_out), .en(or_4_out), .clk(clk), .Q(R12));  // open: clr
  or or_4 (or_4_out, rst, and_4_out);
  Register #(.width(32)) register_5 (.D(multiplexer_1_out), .en(or_5_out), .clk(clk), .Q(R16));  // open: clr
  or or_5 (or_5_out, rst, and_5_out);
  Register #(.width(32)) register_6 (.D(multiplexer_1_out), .en(or_6_out), .clk(clk), .Q(R20));  // open: clr
  or or_6 (or_6_out, rst, and_6_out);
  Register #(.width(32)) register_7 (.D(multiplexer_1_out), .en(or_7_out), .clk(clk), .Q(R24));  // open: clr
  or or_7 (or_7_out, rst, and_7_out);
  Register #(.width(32)) register_8 (.D(multiplexer_1_out), .en(or_8_out), .clk(clk), .Q(R28));  // open: clr
  or or_8 (or_8_out, rst, and_8_out);
  Multiplexer #(.select(3), .width(32)) multiplexer_2 (
    .in0({32{1'b0}}), .in1(R4), .in2(R8), .in3(R12), .in4(R16), .in5(R20), .in6(R24), .in7(R28),
    .out(multiplexer_2_out), .sel(Aread0[4:2]));
  Multiplexer #(.select(3), .width(32)) multiplexer_3 (
    .in0({32{1'b0}}), .in1(R4), .in2(R8), .in3(R12), .in4(R16), .in5(R20), .in6(R24), .in7(R28),
    .out(multiplexer_3_out), .sel(Aread1[4:2]));
  and and_9 (and_9_out, decoder_2_out1, decoder_1_out0);
  and and_10 (and_10_out, decoder_2_out1, decoder_1_out1);
  and and_11 (and_11_out, decoder_2_out1, decoder_1_out2);
  and and_12 (and_12_out, decoder_2_out1, decoder_1_out3);
  and and_13 (and_13_out, decoder_2_out1, decoder_1_out4);
  and and_14 (and_14_out, decoder_2_out1, decoder_1_out5);
  and and_15 (and_15_out, decoder_2_out1, decoder_1_out6);
  and and_16 (and_16_out, decoder_2_out1, decoder_1_out7);
  Register #(.width(32)) register_9 (.D(multiplexer_1_out), .en(or_9_out), .clk(clk), .Q(R1));  // open: clr
  or or_9 (or_9_out, rst, and_9_out);
  Register #(.width(32)) register_10 (.D(multiplexer_1_out), .en(or_10_out), .clk(clk), .Q(R5));  // open: clr
  or or_10 (or_10_out, rst, and_10_out);
  Register #(.width(32)) register_11 (.D(multiplexer_1_out), .en(or_11_out), .clk(clk), .Q(R9));  // open: clr
  or or_11 (or_11_out, rst, and_11_out);
  Register #(.width(32)) register_12 (.D(multiplexer_1_out), .en(or_12_out), .clk(clk), .Q(R13));  // open: clr
  or or_12 (or_12_out, rst, and_12_out);
  Register #(.width(32)) register_13 (.D(multiplexer_1_out), .en(or_13_out), .clk(clk), .Q(R17));  // open: clr
  or or_13 (or_13_out, rst, and_13_out);
  Register #(.width(32)) register_14 (.D(multiplexer_1_out), .en(or_14_out), .clk(clk), .Q(R21));  // open: clr
  or or_14 (or_14_out, rst, and_14_out);
  Register #(.width(32)) register_15 (.D(multiplexer_1_out), .en(or_15_out), .clk(clk), .Q(R25));  // open: clr
  or or_15 (or_15_out, rst, and_15_out);
  Register #(.width(32)) register_16 (.D(multiplexer_1_out), .en(or_16_out), .clk(clk), .Q(R29));  // open: clr
  or or_16 (or_16_out, rst, and_16_out);
  Multiplexer #(.select(3), .width(32)) multiplexer_4 (
    .in0(R1), .in1(R5), .in2(R9), .in3(R13), .in4(R17), .in5(R21), .in6(R25), .in7(R29),
    .out(multiplexer_4_out), .sel(Aread0[4:2]));
  Multiplexer #(.select(3), .width(32)) multiplexer_5 (
    .in0(R1), .in1(R5), .in2(R9), .in3(R13), .in4(R17), .in5(R21), .in6(R25), .in7(R29),
    .out(multiplexer_5_out), .sel(Aread1[4:2]));
  Register #(.width(32)) register_17 (.D(multiplexer_1_out), .en(or_17_out), .clk(clk), .Q(R2));  // open: clr
  or or_17 (or_17_out, rst, and_17_out);
  and and_17 (and_17_out, decoder_2_out2, decoder_1_out0);
  Register #(.width(32)) register_18 (.D(multiplexer_1_out), .en(or_18_out), .clk(clk), .Q(R6));  // open: clr
  or or_18 (or_18_out, rst, and_18_out);
  and and_18 (and_18_out, decoder_2_out2, decoder_1_out1);
  Register #(.width(32)) register_19 (.D(multiplexer_1_out), .en(or_19_out), .clk(clk), .Q(R10));  // open: clr
  or or_19 (or_19_out, rst, and_19_out);
  and and_19 (and_19_out, decoder_2_out2, decoder_1_out2);
  Register #(.width(32)) register_20 (.D(multiplexer_1_out), .en(or_20_out), .clk(clk), .Q(R14));  // open: clr
  or or_20 (or_20_out, rst, and_20_out);
  and and_20 (and_20_out, decoder_2_out2, decoder_1_out3);
  Register #(.width(32)) register_21 (.D(multiplexer_1_out), .en(or_21_out), .clk(clk), .Q(R18));  // open: clr
  or or_21 (or_21_out, rst, and_21_out);
  and and_21 (and_21_out, decoder_2_out2, decoder_1_out4);
  Register #(.width(32)) register_22 (.D(multiplexer_1_out), .en(or_22_out), .clk(clk), .Q(R22));  // open: clr
  or or_22 (or_22_out, rst, and_22_out);
  and and_22 (and_22_out, decoder_2_out2, decoder_1_out5);
  Register #(.width(32)) register_23 (.D(multiplexer_1_out), .en(or_23_out), .clk(clk), .Q(R26));  // open: clr
  or or_23 (or_23_out, rst, and_23_out);
  and and_23 (and_23_out, decoder_2_out2, decoder_1_out6);
  Register #(.width(32)) register_24 (.D(multiplexer_1_out), .en(or_24_out), .clk(clk), .Q(R30));  // open: clr
  or or_24 (or_24_out, rst, and_24_out);
  and and_24 (and_24_out, decoder_2_out2, decoder_1_out7);
  Multiplexer #(.select(3), .width(32)) multiplexer_6 (
    .in0(R2), .in1(R6), .in2(R10), .in3(R14), .in4(R18), .in5(R22), .in6(R26), .in7(R30),
    .out(multiplexer_6_out), .sel(Aread0[4:2]));
  Multiplexer #(.select(3), .width(32)) multiplexer_7 (
    .in0(R2), .in1(R6), .in2(R10), .in3(R14), .in4(R18), .in5(R22), .in6(R26), .in7(R30),
    .out(multiplexer_7_out), .sel(Aread1[4:2]));
  Register #(.width(32)) register_25 (.D(multiplexer_1_out), .en(or_25_out), .clk(clk), .Q(R3));  // open: clr
  or or_25 (or_25_out, rst, and_25_out);
  and and_25 (and_25_out, decoder_2_out3, decoder_1_out0);
  Register #(.width(32)) register_26 (.D(multiplexer_1_out), .en(or_26_out), .clk(clk), .Q(R7));  // open: clr
  or or_26 (or_26_out, rst, and_26_out);
  and and_26 (and_26_out, decoder_2_out3, decoder_1_out1);
  Register #(.width(32)) register_27 (.D(multiplexer_1_out), .en(or_27_out), .clk(clk), .Q(R11));  // open: clr
  or or_27 (or_27_out, rst, and_27_out);
  and and_27 (and_27_out, decoder_2_out3, decoder_1_out2);
  Register #(.width(32)) register_28 (.D(multiplexer_1_out), .en(or_28_out), .clk(clk), .Q(R15));  // open: clr
  or or_28 (or_28_out, rst, and_28_out);
  and and_28 (and_28_out, decoder_2_out3, decoder_1_out3);
  Register #(.width(32)) register_29 (.D(multiplexer_1_out), .en(or_29_out), .clk(clk), .Q(R19));  // open: clr
  or or_29 (or_29_out, rst, and_29_out);
  and and_29 (and_29_out, decoder_2_out3, decoder_1_out4);
  Register #(.width(32)) register_30 (.D(multiplexer_1_out), .en(or_30_out), .clk(clk), .Q(R23));  // open: clr
  or or_30 (or_30_out, rst, and_30_out);
  and and_30 (and_30_out, decoder_2_out3, decoder_1_out5);
  Register #(.width(32)) register_31 (.D(multiplexer_1_out), .en(or_31_out), .clk(clk), .Q(R27));  // open: clr
  or or_31 (or_31_out, rst, and_31_out);
  and and_31 (and_31_out, decoder_2_out3, decoder_1_out6);
  Register #(.width(32)) register_32 (.D(multiplexer_1_out), .en(or_32_out), .clk(clk), .Q(R31));  // open: clr
  or or_32 (or_32_out, rst, and_32_out);
  and and_32 (and_32_out, decoder_2_out3, decoder_1_out7);
  Multiplexer #(.select(3), .width(32)) multiplexer_8 (
    .in0(R3), .in1(R7), .in2(R11), .in3(R15), .in4(R19), .in5(R23), .in6(R27), .in7(R31),
    .out(multiplexer_8_out), .sel(Aread0[4:2]));
  Multiplexer #(.select(3), .width(32)) multiplexer_9 (
    .in0(R3), .in1(R7), .in2(R11), .in3(R15), .in4(R19), .in5(R23), .in6(R27), .in7(R31),
    .out(multiplexer_9_out), .sel(Aread1[4:2]));
  Multiplexer #(.select(2), .width(32)) multiplexer_10 (
    .in0(multiplexer_2_out), .in1(multiplexer_4_out), .in2(multiplexer_6_out), .in3(multiplexer_8_out),
    .out(Dread0), .sel(Aread0[1:0]));
  Multiplexer #(.select(2), .width(32)) multiplexer_11 (
    .in0(multiplexer_3_out), .in1(multiplexer_5_out), .in2(multiplexer_7_out), .in3(multiplexer_9_out),
    .out(Dread1), .sel(Aread1[1:0]));

  // Notes on the sheet:
  //   Field Template
endmodule

module alu_ctrl_circuit (
  input  [5:0] funct,
  input  [1:0] ALUop,
  output [5:0] Operation_number
);

  Multiplexer #(.select(2), .width(6)) multiplexer_1 (
    .in0({6{1'b0}}), .in1(6'b100000), .in2(6'b100010), .in3(funct), .out(Operation_number), .sel(ALUop));
endmodule

module jtag_ram8_128 (
  input  [31:0] Din0,
  input  [31:0] Din1,
  input  [31:0] Din2,
  input  clk,
  input  Jen,
  input  [31:0] Din3,
  input  [31:0] Jin,
  input  [1:0] Wen,
  input  [2:0] Addr,
  output [31:0] Dout3,
  output [31:0] Dout2,
  output [31:0] Dout1,
  output [31:0] Dout0,
  output [31:0] Jout
);

  wire comparator_1_eq, comparator_2_eq, decoder_1_out0, decoder_1_out1, decoder_2_out0, decoder_2_out1,
       decoder_2_out2, decoder_2_out3, decoder_2_out4, decoder_2_out5, decoder_2_out6, decoder_2_out7,
       multiplexer_1_out, multiplexer_2_out, multiplexer_3_out, multiplexer_4_out, multiplexer_5_out,
       multiplexer_6_out, multiplexer_7_out, multiplexer_8_out, or_1_out, or_2_out, or_3_out, or_4_out,
       or_5_out, or_6_out, or_7_out, or_8_out;
  wire [31:0] M0, M1, M2, M3, M4, M5, M6, multiplexer_9_out, multiplexer_10_out, multiplexer_11_out,
       multiplexer_12_out, multiplexer_13_out, multiplexer_14_out, multiplexer_15_out, multiplexer_16_out,
       multiplexer_17_out, multiplexer_18_out, multiplexer_19_out, multiplexer_20_out, multiplexer_21_out;

  Comparator #(.mode("unsigned"), .width(2)) comparator_1 (.a(Wen), .b(2'b11), .eq(comparator_1_eq));  // open: gt, lt
  Comparator #(.mode("unsigned"), .width(2)) comparator_2 (.a(Wen), .b(2'b01), .eq(comparator_2_eq));  // open: gt, lt
  Decoder decoder_1 (.out0(decoder_1_out0), .out1(decoder_1_out1), .sel(Addr[2]), .en(comparator_1_eq));
  Decoder #(.select(3)) decoder_2 (
    .out0(decoder_2_out0), .out1(decoder_2_out1), .out2(decoder_2_out2), .out3(decoder_2_out3),
    .out4(decoder_2_out4), .out5(decoder_2_out5), .out6(decoder_2_out6), .out7(decoder_2_out7), .sel(Addr),
    .en(comparator_2_eq));
  Multiplexer multiplexer_1 (
    .in0(decoder_2_out0), .in1(decoder_1_out0), .out(multiplexer_1_out), .sel(comparator_1_eq));
  Multiplexer multiplexer_2 (
    .in0(decoder_2_out1), .in1(decoder_1_out0), .out(multiplexer_2_out), .sel(comparator_1_eq));
  Multiplexer multiplexer_3 (
    .in0(decoder_2_out2), .in1(decoder_1_out0), .out(multiplexer_3_out), .sel(comparator_1_eq));
  Multiplexer multiplexer_4 (
    .in0(decoder_2_out3), .in1(decoder_1_out0), .out(multiplexer_4_out), .sel(comparator_1_eq));
  Multiplexer multiplexer_5 (
    .in0(decoder_2_out4), .in1(decoder_1_out1), .out(multiplexer_5_out), .sel(comparator_1_eq));
  Multiplexer multiplexer_6 (
    .in0(decoder_2_out5), .in1(decoder_1_out1), .out(multiplexer_6_out), .sel(comparator_1_eq));
  Multiplexer multiplexer_7 (
    .in0(decoder_2_out6), .in1(decoder_1_out1), .out(multiplexer_7_out), .sel(comparator_1_eq));
  Multiplexer multiplexer_8 (
    .in0(decoder_2_out7), .in1(decoder_1_out1), .out(multiplexer_8_out), .sel(comparator_1_eq));
  Multiplexer #(.width(32)) multiplexer_9 (.in0(Din0), .in1(Din1), .out(multiplexer_9_out), .sel(comparator_1_eq));
  Multiplexer #(.width(32)) multiplexer_10 (.in0(Din0), .in1(Din2), .out(multiplexer_10_out), .sel(comparator_1_eq));
  Multiplexer #(.width(32)) multiplexer_11 (.in0(Din0), .in1(Din3), .out(multiplexer_11_out), .sel(comparator_1_eq));
  Multiplexer #(.width(32)) multiplexer_12 (.in0(Din0), .in1(Jin), .out(multiplexer_12_out), .sel(Jen));
  Multiplexer #(.width(32)) multiplexer_13 (.in0(multiplexer_9_out), .in1(M0), .out(multiplexer_13_out), .sel(Jen));
  Multiplexer #(.width(32)) multiplexer_14 (.in0(multiplexer_10_out), .in1(M1), .out(multiplexer_14_out), .sel(Jen));
  Multiplexer #(.width(32)) multiplexer_15 (.in0(multiplexer_11_out), .in1(M2), .out(multiplexer_15_out), .sel(Jen));
  Multiplexer #(.width(32)) multiplexer_16 (.in0(Din0), .in1(M3), .out(multiplexer_16_out), .sel(Jen));
  Multiplexer #(.width(32)) multiplexer_17 (.in0(multiplexer_9_out), .in1(M4), .out(multiplexer_17_out), .sel(Jen));
  Multiplexer #(.width(32)) multiplexer_18 (.in0(multiplexer_10_out), .in1(M5), .out(multiplexer_18_out), .sel(Jen));
  Multiplexer #(.width(32)) multiplexer_19 (.in0(multiplexer_11_out), .in1(M6), .out(multiplexer_19_out), .sel(Jen));
  Register #(.width(32)) register_1 (.D(multiplexer_12_out), .en(or_1_out), .clk(clk), .Q(M0));  // open: clr
  or or_1 (or_1_out, Jen, multiplexer_1_out);
  Register #(.width(32)) register_2 (.D(multiplexer_13_out), .en(or_2_out), .clk(clk), .Q(M1));  // open: clr
  or or_2 (or_2_out, Jen, multiplexer_2_out);
  Register #(.width(32)) register_3 (.D(multiplexer_14_out), .en(or_3_out), .clk(clk), .Q(M2));  // open: clr
  or or_3 (or_3_out, Jen, multiplexer_3_out);
  Register #(.width(32)) register_4 (.D(multiplexer_15_out), .en(or_4_out), .clk(clk), .Q(M3));  // open: clr
  or or_4 (or_4_out, Jen, multiplexer_4_out);
  Register #(.width(32)) register_5 (.D(multiplexer_16_out), .en(or_5_out), .clk(clk), .Q(M4));  // open: clr
  or or_5 (or_5_out, Jen, multiplexer_5_out);
  Register #(.width(32)) register_6 (.D(multiplexer_17_out), .en(or_6_out), .clk(clk), .Q(M5));  // open: clr
  or or_6 (or_6_out, Jen, multiplexer_6_out);
  Register #(.width(32)) register_7 (.D(multiplexer_18_out), .en(or_7_out), .clk(clk), .Q(M6));  // open: clr
  or or_7 (or_7_out, Jen, multiplexer_7_out);
  Register #(.width(32)) register_8 (.D(multiplexer_19_out), .en(or_8_out), .clk(clk), .Q(Jout));  // open: clr
  or or_8 (or_8_out, Jen, multiplexer_8_out);
  Multiplexer #(.select(3), .width(32)) multiplexer_20 (
    .in0(M0), .in1(M1), .in2(M2), .in3(M3), .in4(M4), .in5(M5), .in6(M6), .in7(Jout),
    .out(multiplexer_20_out), .sel(Addr));
  Multiplexer #(.width(32)) multiplexer_21 (.in0(M0), .in1(M4), .out(multiplexer_21_out), .sel(Addr[2]));
  Multiplexer #(.width(32)) multiplexer_22 (.in0(M1), .in1(M5), .out(Dout1), .sel(Addr[2]));
  Multiplexer #(.width(32)) multiplexer_23 (.in0(M2), .in1(M6), .out(Dout2), .sel(Addr[2]));
  Multiplexer #(.width(32)) multiplexer_24 (.in0(M3), .in1(Jout), .out(Dout3), .sel(Addr[2]));
  Multiplexer #(.width(32)) multiplexer_25 (
    .in0(multiplexer_20_out), .in1(multiplexer_21_out), .out(Dout0), .sel(Wen[1]));

  // Other names for the same wires on the sheet: M7[31:0] = Jout
endmodule

module jtag_ram64_128 (
  input  [31:0] Din0,
  input  [31:0] Din1,
  input  [31:0] Din2,
  input  clk,
  input  [31:0] Din3,
  input  Jen,
  input  [31:0] Jin,
  input  [1:0] Wen,
  input  [5:0] Addr,
  output [31:0] Dout3,
  output [31:0] Dout2,
  output [31:0] Dout1,
  output [31:0] Jout,
  output [31:0] Dout0
);

  wire [0:0] decoder_1_out0, decoder_1_out1, decoder_1_out2, decoder_1_out3, decoder_1_out4, decoder_1_out5,
       decoder_1_out6, decoder_1_out7;
  wire [31:0] b0_dout0, b0_dout1, b0_dout2, b0_dout3, b1_dout0, b1_dout1, b1_dout2, b1_dout3, b2_dout0,
       b2_dout1, b2_dout2, b2_dout3, b3_dout0, b3_dout1, b3_dout2, b3_dout3, b4_dout0, b4_dout1, b4_dout2,
       b4_dout3, b5_dout0, b5_dout1, b5_dout2, b5_dout3, b6_dout0, b6_dout1, b6_dout2, b6_dout3, b7_dout0,
       b7_dout1, b7_dout2, b7_dout3;

  Decoder #(.select(3)) decoder_1 (
    .out0(decoder_1_out0[0]), .out1(decoder_1_out1[0]), .out2(decoder_1_out2[0]), .out3(decoder_1_out3[0]),
    .out4(decoder_1_out4[0]), .out5(decoder_1_out5[0]), .out6(decoder_1_out6[0]), .out7(decoder_1_out7[0]),
    .sel(Addr[5:3]), .en(Wen[0]));
  jtag_ram8_128 b0 (
    .Din0(Din0), .Din1(Din1), .Din2(Din2), .clk(clk), .Jen(Jen), .Din3(Din3), .Jin(Jin),
    .Wen({Wen[1], decoder_1_out0[0]}), .Addr(Addr[2:0]), .Dout3(b0_dout3), .Dout2(b0_dout2),
    .Dout1(b0_dout1), .Dout0(b0_dout0));  // open: Jout
  jtag_ram8_128 b1 (
    .Din0(Din0), .Din1(Din1), .Din2(Din2), .clk(clk), .Jen(Jen), .Din3(Din3), .Jin(Jin),
    .Wen({Wen[1], decoder_1_out1[0]}), .Addr(Addr[2:0]), .Dout3(b1_dout3), .Dout2(b1_dout2),
    .Dout1(b1_dout1), .Dout0(b1_dout0));  // open: Jout
  jtag_ram8_128 b2 (
    .Din0(Din0), .Din1(Din1), .Din2(Din2), .clk(clk), .Jen(Jen), .Din3(Din3), .Jin(Jin),
    .Wen({Wen[1], decoder_1_out2[0]}), .Addr(Addr[2:0]), .Dout3(b2_dout3), .Dout2(b2_dout2),
    .Dout1(b2_dout1), .Dout0(b2_dout0));  // open: Jout
  jtag_ram8_128 b3 (
    .Din0(Din0), .Din1(Din1), .Din2(Din2), .clk(clk), .Jen(Jen), .Din3(Din3), .Jin(Jin),
    .Wen({Wen[1], decoder_1_out3[0]}), .Addr(Addr[2:0]), .Dout3(b3_dout3), .Dout2(b3_dout2),
    .Dout1(b3_dout1), .Dout0(b3_dout0));  // open: Jout
  jtag_ram8_128 b4 (
    .Din0(Din0), .Din1(Din1), .Din2(Din2), .clk(clk), .Jen(Jen), .Din3(Din3), .Jin(Jin),
    .Wen({Wen[1], decoder_1_out4[0]}), .Addr(Addr[2:0]), .Dout3(b4_dout3), .Dout2(b4_dout2),
    .Dout1(b4_dout1), .Dout0(b4_dout0));  // open: Jout
  jtag_ram8_128 b5 (
    .Din0(Din0), .Din1(Din1), .Din2(Din2), .clk(clk), .Jen(Jen), .Din3(Din3), .Jin(Jin),
    .Wen({Wen[1], decoder_1_out5[0]}), .Addr(Addr[2:0]), .Dout3(b5_dout3), .Dout2(b5_dout2),
    .Dout1(b5_dout1), .Dout0(b5_dout0));  // open: Jout
  jtag_ram8_128 b6 (
    .Din0(Din0), .Din1(Din1), .Din2(Din2), .clk(clk), .Jen(Jen), .Din3(Din3), .Jin(Jin),
    .Wen({Wen[1], decoder_1_out6[0]}), .Addr(Addr[2:0]), .Dout3(b6_dout3), .Dout2(b6_dout2),
    .Dout1(b6_dout1), .Dout0(b6_dout0));  // open: Jout
  jtag_ram8_128 b7 (
    .Din0(Din0), .Din1(Din1), .Din2(Din2), .clk(clk), .Jen(Jen), .Din3(Din3), .Jin(Jin),
    .Wen({Wen[1], decoder_1_out7[0]}), .Addr(Addr[2:0]), .Dout3(b7_dout3), .Dout2(b7_dout2),
    .Dout1(b7_dout1), .Dout0(b7_dout0), .Jout(Jout));
  Multiplexer #(.select(3), .width(32)) multiplexer_1 (
    .in0(b0_dout3), .in1(b1_dout3), .in2(b2_dout3), .in3(b3_dout3), .in4(b4_dout3), .in5(b5_dout3),
    .in6(b6_dout3), .in7(b7_dout3), .out(Dout3), .sel(Addr[5:3]));
  Multiplexer #(.select(3), .width(32)) multiplexer_2 (
    .in0(b0_dout2), .in1(b1_dout2), .in2(b2_dout2), .in3(b3_dout2), .in4(b4_dout2), .in5(b5_dout2),
    .in6(b6_dout2), .in7(b7_dout2), .out(Dout2), .sel(Addr[5:3]));
  Multiplexer #(.select(3), .width(32)) multiplexer_3 (
    .in0(b0_dout1), .in1(b1_dout1), .in2(b2_dout1), .in3(b3_dout1), .in4(b4_dout1), .in5(b5_dout1),
    .in6(b6_dout1), .in7(b7_dout1), .out(Dout1), .sel(Addr[5:3]));
  Multiplexer #(.select(3), .width(32)) multiplexer_4 (
    .in0(b0_dout0), .in1(b1_dout0), .in2(b2_dout0), .in3(b3_dout0), .in4(b4_dout0), .in5(b5_dout0),
    .in6(b6_dout0), .in7(b7_dout0), .out(Dout0), .sel(Addr[5:3]));
endmodule

module jtag_ram512_128 (
  input  [31:0] Din0,
  input  [31:0] Din1,
  input  [31:0] Din2,
  input  [31:0] Din3,
  input  clk,
  input  Jen,
  input  [31:0] Jin,
  input  [1:0] Wen,
  input  [8:0] Addr,
  output [31:0] Dout3,
  output [31:0] Dout2,
  output [31:0] Dout1,
  output [31:0] Dout0,
  output [31:0] Jout
);

  wire [0:0] decoder_1_out0, decoder_1_out1, decoder_1_out2, decoder_1_out3, decoder_1_out4, decoder_1_out5,
       decoder_1_out6, decoder_1_out7;
  wire [31:0] c0_dout0, c0_dout1, c0_dout2, c0_dout3, c1_dout0, c1_dout1, c1_dout2, c1_dout3, c2_dout0,
       c2_dout1, c2_dout2, c2_dout3, c3_dout0, c3_dout1, c3_dout2, c3_dout3, c4_dout0, c4_dout1, c4_dout2,
       c4_dout3, c5_dout0, c5_dout1, c5_dout2, c5_dout3, c6_dout0, c6_dout1, c6_dout2, c6_dout3, c7_dout0,
       c7_dout1, c7_dout2, c7_dout3;

  Decoder #(.select(3)) decoder_1 (
    .out0(decoder_1_out0[0]), .out1(decoder_1_out1[0]), .out2(decoder_1_out2[0]), .out3(decoder_1_out3[0]),
    .out4(decoder_1_out4[0]), .out5(decoder_1_out5[0]), .out6(decoder_1_out6[0]), .out7(decoder_1_out7[0]),
    .sel(Addr[8:6]), .en(Wen[0]));
  jtag_ram64_128 c0 (
    .Din0(Din0), .Din1(Din1), .Din2(Din2), .clk(clk), .Din3(Din3), .Jen(Jen), .Jin(Jin),
    .Wen({Wen[1], decoder_1_out0[0]}), .Addr(Addr[5:0]), .Dout3(c0_dout3), .Dout2(c0_dout2),
    .Dout1(c0_dout1), .Dout0(c0_dout0));  // open: Jout
  jtag_ram64_128 c1 (
    .Din0(Din0), .Din1(Din1), .Din2(Din2), .clk(clk), .Din3(Din3), .Jen(Jen), .Jin(Jin),
    .Wen({Wen[1], decoder_1_out1[0]}), .Addr(Addr[5:0]), .Dout3(c1_dout3), .Dout2(c1_dout2),
    .Dout1(c1_dout1), .Dout0(c1_dout0));  // open: Jout
  jtag_ram64_128 c2 (
    .Din0(Din0), .Din1(Din1), .Din2(Din2), .clk(clk), .Din3(Din3), .Jen(Jen), .Jin(Jin),
    .Wen({Wen[1], decoder_1_out2[0]}), .Addr(Addr[5:0]), .Dout3(c2_dout3), .Dout2(c2_dout2),
    .Dout1(c2_dout1), .Dout0(c2_dout0));  // open: Jout
  jtag_ram64_128 c3 (
    .Din0(Din0), .Din1(Din1), .Din2(Din2), .clk(clk), .Din3(Din3), .Jen(Jen), .Jin(Jin),
    .Wen({Wen[1], decoder_1_out3[0]}), .Addr(Addr[5:0]), .Dout3(c3_dout3), .Dout2(c3_dout2),
    .Dout1(c3_dout1), .Dout0(c3_dout0));  // open: Jout
  jtag_ram64_128 c4 (
    .Din0(Din0), .Din1(Din1), .Din2(Din2), .clk(clk), .Din3(Din3), .Jen(Jen), .Jin(Jin),
    .Wen({Wen[1], decoder_1_out4[0]}), .Addr(Addr[5:0]), .Dout3(c4_dout3), .Dout2(c4_dout2),
    .Dout1(c4_dout1), .Dout0(c4_dout0));  // open: Jout
  jtag_ram64_128 c5 (
    .Din0(Din0), .Din1(Din1), .Din2(Din2), .clk(clk), .Din3(Din3), .Jen(Jen), .Jin(Jin),
    .Wen({Wen[1], decoder_1_out5[0]}), .Addr(Addr[5:0]), .Dout3(c5_dout3), .Dout2(c5_dout2),
    .Dout1(c5_dout1), .Dout0(c5_dout0));  // open: Jout
  jtag_ram64_128 c6 (
    .Din0(Din0), .Din1(Din1), .Din2(Din2), .clk(clk), .Din3(Din3), .Jen(Jen), .Jin(Jin),
    .Wen({Wen[1], decoder_1_out6[0]}), .Addr(Addr[5:0]), .Dout3(c6_dout3), .Dout2(c6_dout2),
    .Dout1(c6_dout1), .Dout0(c6_dout0));  // open: Jout
  jtag_ram64_128 c7 (
    .Din0(Din0), .Din1(Din1), .Din2(Din2), .clk(clk), .Din3(Din3), .Jen(Jen), .Jin(Jin),
    .Wen({Wen[1], decoder_1_out7[0]}), .Addr(Addr[5:0]), .Dout3(c7_dout3), .Dout2(c7_dout2),
    .Dout1(c7_dout1), .Jout(Jout), .Dout0(c7_dout0));
  Multiplexer #(.select(3), .width(32)) multiplexer_1 (
    .in0(c0_dout3), .in1(c1_dout3), .in2(c2_dout3), .in3(c3_dout3), .in4(c4_dout3), .in5(c5_dout3),
    .in6(c6_dout3), .in7(c7_dout3), .out(Dout3), .sel(Addr[8:6]));
  Multiplexer #(.select(3), .width(32)) multiplexer_2 (
    .in0(c0_dout2), .in1(c1_dout2), .in2(c2_dout2), .in3(c3_dout2), .in4(c4_dout2), .in5(c5_dout2),
    .in6(c6_dout2), .in7(c7_dout2), .out(Dout2), .sel(Addr[8:6]));
  Multiplexer #(.select(3), .width(32)) multiplexer_3 (
    .in0(c0_dout1), .in1(c1_dout1), .in2(c2_dout1), .in3(c3_dout1), .in4(c4_dout1), .in5(c5_dout1),
    .in6(c6_dout1), .in7(c7_dout1), .out(Dout1), .sel(Addr[8:6]));
  Multiplexer #(.select(3), .width(32)) multiplexer_4 (
    .in0(c0_dout0), .in1(c1_dout0), .in2(c2_dout0), .in3(c3_dout0), .in4(c4_dout0), .in5(c5_dout0),
    .in6(c6_dout0), .in7(c7_dout0), .out(Dout0), .sel(Addr[8:6]));
endmodule

module div_circuit (
  input  start,
  input  [31:0] dividend,
  input  [31:0] divisor,
  input  clk,
  output [31:0] remainder,
  output [31:0] quotient,
  output done
);

  wire and_1_out, and_2_out, and_3_out, and_4_out, and_5_out, comparator_1_eq, comparator_1_gt,
       comparator_1_lt, comparator_2_eq, comparator_2_gt, FinalBlock_q, multiplexer_3_out, or_1_out,
       or_2_out, or_3_out, or_4_out, or_5_out, or_6_out, or_8_out, StartBlock_q;
  wire [1:0] ShiftBlock_q;
  wire [7:0] counter_q, multiplexer_2_out, multiplexer_6_out, subtractor_1_out;
  wire [31:0] adder_1_out, b_q, multiplexer_1_out, multiplexer_4_out, multiplexer_5_out, or_7_out,
       shifter_1_out, shifter_2_out, shifter_3_out, subtractor_2_out;

  and and_1 (and_1_out, ShiftBlock_q[1], comparator_2_gt);
  and and_2 (and_2_out, ShiftBlock_q[0], comparator_1_lt, comparator_2_gt);
  and and_3 (and_3_out, ShiftBlock_q[1], comparator_2_eq);
  and and_4 (and_4_out, ShiftBlock_q[0], comparator_1_lt, comparator_2_eq);
  D_Flip_Flop StartBlock (.D(1'b0), .clk(clk), .Q(StartBlock_q), .preset(start));  // open: Qn, reset
  D_Flip_Flop ShiftBlock (.D(or_1_out), .clk(clk), .Q(ShiftBlock_q[0]), .reset(start));  // open: Qn, preset
  or or_1 (or_1_out, StartBlock_q, and_1_out, and_2_out);
  D_Flip_Flop SubtractBlock (.D(and_5_out), .clk(clk), .Q(ShiftBlock_q[1]), .reset(start));  // open: Qn, preset
  and and_5 (and_5_out, ShiftBlock_q[0], or_8_out);
  D_Flip_Flop FinalBlock (.D(or_2_out), .clk(clk), .Q(FinalBlock_q), .preset(FinalBlock_q), .reset(start));  // open: Qn
  or or_2 (or_2_out, and_3_out, and_4_out);
  or or_3 (or_3_out, ShiftBlock_q[0], StartBlock_q, ShiftBlock_q[1]);
  or or_4 (or_4_out, ShiftBlock_q[1], ShiftBlock_q[0], StartBlock_q);
  or or_5 (or_5_out, StartBlock_q, FinalBlock_q);
  Multiplexer #(.select(2), .width(32)) multiplexer_1 (
    .in0(dividend), .in1(shifter_3_out), .in2(or_7_out), .out(multiplexer_1_out), .sel(ShiftBlock_q));  // open: in3
  Multiplexer #(.width(8)) multiplexer_2 (
    .in0(8'h20), .in1(subtractor_1_out), .out(multiplexer_2_out), .sel(ShiftBlock_q[0]));
  or or_6 (or_6_out, StartBlock_q, ShiftBlock_q[0]);
  Multiplexer multiplexer_3 (.in0(1'b1), .in1(1'b0), .out(multiplexer_3_out), .sel(StartBlock_q));
  Multiplexer #(.width(32)) multiplexer_4 (
    .in0(subtractor_2_out), .in1(adder_1_out), .out(multiplexer_4_out), .sel(ShiftBlock_q[0]));
  Multiplexer #(.width(32)) multiplexer_5 (
    .in0(multiplexer_4_out), .in1({32{1'b0}}), .out(multiplexer_5_out), .sel(StartBlock_q));
  Register #(.width(32)) a (.D(multiplexer_5_out), .en(or_3_out), .clk(clk), .Q(remainder));  // open: clr
  Register #(.width(32)) q (.D(multiplexer_1_out), .en(or_4_out), .clk(clk), .Q(quotient));  // open: clr
  Register #(.width(32)) b (.D(divisor), .en(StartBlock_q), .clk(clk), .Q(b_q));  // open: clr
  Register counter (.D(multiplexer_2_out), .en(or_6_out), .clk(clk), .Q(counter_q));  // open: clr
  Register #(.width(1)) d (.D(multiplexer_3_out), .en(or_5_out), .clk(clk), .Q(done), .clr(start));
  Subtractor subtractor_1 (.a(counter_q), .b(8'h1), .out(subtractor_1_out));  // open: bin, bout
  Shifter #(.width(32)) shifter_1 (.in(remainder), .\dist (5'b00001), .out(shifter_1_out));
  Shifter #(.shift("lr"), .width(32)) shifter_2 (.in(quotient), .\dist ({5{1'b1}}), .out(shifter_2_out));
  Shifter #(.width(32)) shifter_3 (.in(quotient), .\dist (5'b00001), .out(shifter_3_out));
  assign or_7_out = quotient | 32'h1;  // OR_Gate or_7, 32 bits wide
  Adder #(.width(32)) adder_1 (.a(shifter_1_out), .b(shifter_2_out), .out(adder_1_out));  // open: cin, cout
  Multiplexer #(.width(8)) multiplexer_6 (
    .in0(subtractor_1_out), .in1(counter_q), .out(multiplexer_6_out), .sel(ShiftBlock_q[1]));
  or or_8 (or_8_out, comparator_1_gt, comparator_1_eq);
  Comparator #(.mode("unsigned"), .width(32)) comparator_1 (
    .a(adder_1_out), .b(b_q), .gt(comparator_1_gt), .eq(comparator_1_eq), .lt(comparator_1_lt));
  Subtractor #(.width(32)) subtractor_2 (.a(remainder), .b(b_q), .out(subtractor_2_out));  // open: bin, bout
  Comparator #(.mode("unsigned")) comparator_2 (
    .a(multiplexer_6_out), .b({8{1'b0}}), .gt(comparator_2_gt), .eq(comparator_2_eq));  // open: lt
endmodule

module mul_circuit (
  input  [31:0] multiplicand,
  input  [31:0] multiplierr,
  output [31:0] res_low
);

  Multiplier #(.mode("twosComplement"), .width(32)) multiplier_1 (
    .a(multiplicand), .b(multiplierr), .out(res_low));  // open: cin, cout
endmodule

module add_circuit (
  input  [31:0] a,
  input  [31:0] b,
  output done,
  output [31:0] res_low
);

  Adder #(.width(32)) adder_1 (.a(a), .b(b), .out(res_low));  // open: cin, cout

  assign done = 1'b1;

  // Notes on the sheet:
  //   a: initial=0x932d612
  //   b: initial=0xc7ecdb8f
endmodule

module sub_circuit (
  input  [31:0] a,
  input  [31:0] b,
  output [31:0] res_high,
  output [31:0] res_low,
  output done
);

  wire [63:0] bit_extender_1_out, bit_extender_2_out;

  assign bit_extender_1_out = {{32{1'b0}}, a};  // Bit_Extender bit_extender_1
  assign bit_extender_2_out = {{32{1'b0}}, b};  // Bit_Extender bit_extender_2
  Subtractor #(.width(64)) subtractor_1 (
    .a(bit_extender_1_out), .b(bit_extender_2_out), .out({res_high, res_low}));  // open: bin, bout

  assign done = 1'b1;

  // Notes on the sheet:
  //   a: initial=0x932d612
  //   b: initial=0xc7ecdb8f
endmodule

module and_circuit (
  input  [31:0] a,
  input  [31:0] b,
  output [31:0] res_high,
  output [31:0] res_low,
  output done
);

  assign res_low = a & b;  // AND_Gate and_1, 32 bits wide

  assign done = 1'b1;
  assign res_high = {32{1'b0}};

  // Notes on the sheet:
  //   a: initial=0x932d612
  //   b: initial=0xc7ecdb8f
endmodule

module xor_circuit (
  input  [31:0] a,
  input  [31:0] b,
  output [31:0] res_high,
  output [31:0] res_low,
  output done
);

  assign res_low = a ^ b;  // XOR_Gate xor_1, 32 bits wide

  assign done = 1'b1;
  assign res_high = {32{1'b0}};

  // Notes on the sheet:
  //   a: initial=0x932d612
  //   b: initial=0xc7ecdb8f
endmodule

module or_circuit (
  input  [31:0] a,
  input  [31:0] b,
  output [31:0] res_high,
  output [31:0] res_low,
  output done
);

  assign res_low = a | b;  // OR_Gate or_1, 32 bits wide

  assign done = 1'b1;
  assign res_high = {32{1'b0}};

  // Notes on the sheet:
  //   a: initial=0x932d612
  //   b: initial=0xc7ecdb8f
endmodule

module sll_circuit (
  input  [31:0] a,
  input  [31:0] b,
  output [31:0] res_low,
  output done
);

  wire [4:0] subtractor_1_out;
  wire [31:0] shifter_1_out, shifter_2_out, shifter_3_out;

  Shifter #(.width(32)) shifter_1 (.in(a), .\dist (5'b00001), .out(shifter_1_out));
  Subtractor #(.width(5)) subtractor_1 (.a(b[4:0]), .b(5'b00001), .out(subtractor_1_out));  // open: bin, bout
  Shifter #(.width(32)) shifter_2 (.in(a), .\dist (b[4:0]), .out(shifter_2_out));
  Shifter #(.width(32)) shifter_3 (.in(shifter_1_out), .\dist (subtractor_1_out), .out(shifter_3_out));
  Multiplexer #(.width(32)) multiplexer_1 (.in0(shifter_3_out), .in1(shifter_2_out), .out(res_low), .sel(b[0]));

  assign done = 1'b1;
endmodule

module srl_circuit (
  input  [31:0] a,
  input  [31:0] b,
  output [31:0] res_high,
  output [31:0] res_low,
  output done
);

  wire comparator_1_eq, xor_1_out;
  wire [5:0] subtractor_1_out;
  wire [63:0] bit_extender_1_out, multiplexer_1_out, shifter_1_out, shifter_2_out, shifter_3_out;
  wire [63:32] multiplexer_2_out;

  assign bit_extender_1_out = {{32{1'b0}}, a};  // Bit_Extender bit_extender_1
  Comparator #(.mode("unsigned"), .width(5)) comparator_1 (
    .a(b[4:0]), .b({5{1'b0}}), .eq(comparator_1_eq));  // open: gt, lt
  Shifter #(.shift("lr"), .width(64)) shifter_1 (.in(bit_extender_1_out), .\dist (6'b000001), .out(shifter_1_out));
  Subtractor #(.width(6)) subtractor_1 (.a({1'b0, b[4:0]}), .b(6'b000001), .out(subtractor_1_out));  // open: bin, bout
  Shifter #(.shift("lr"), .width(64)) shifter_2 (.in(bit_extender_1_out), .\dist ({1'b0, b[4:0]}), .out(shifter_2_out));
  Shifter #(.shift("lr"), .width(64)) shifter_3 (.in(shifter_1_out), .\dist (subtractor_1_out), .out(shifter_3_out));
  Multiplexer #(.width(64)) multiplexer_1 (
    .in0(shifter_3_out), .in1(bit_extender_1_out), .out(multiplexer_1_out), .sel(comparator_1_eq));
  xor xor_1 (xor_1_out, b[0], 1'b0);
  Multiplexer #(.width(64)) multiplexer_2 (
    .in0(multiplexer_1_out), .in1(shifter_2_out), .out({multiplexer_2_out, res_low}), .sel(xor_1_out));

  assign done = 1'b1;
  assign res_high = {32{1'b0}};
endmodule

module sra_circuit (
  input  [31:0] a,
  input  [31:0] b,
  output [31:0] res_high,
  output [31:0] res_low,
  output done
);

  wire comparator_1_eq, xor_1_out;
  wire [5:0] subtractor_1_out;
  wire [63:0] bit_extender_1_out, multiplexer_1_out, shifter_1_out, shifter_2_out, shifter_3_out;
  wire [63:32] multiplexer_2_out;

  assign bit_extender_1_out = {{32{a[31]}}, a};  // Bit_Extender bit_extender_1
  Comparator #(.mode("unsigned"), .width(5)) comparator_1 (
    .a(b[4:0]), .b({5{1'b0}}), .eq(comparator_1_eq));  // open: gt, lt
  Shifter #(.shift("lr"), .width(64)) shifter_1 (.in(bit_extender_1_out), .\dist (6'b000001), .out(shifter_1_out));
  Subtractor #(.width(6)) subtractor_1 (.a({1'b0, b[4:0]}), .b(6'b000001), .out(subtractor_1_out));  // open: bin, bout
  Shifter #(.shift("lr"), .width(64)) shifter_2 (.in(bit_extender_1_out), .\dist ({1'b0, b[4:0]}), .out(shifter_2_out));
  Shifter #(.shift("lr"), .width(64)) shifter_3 (.in(shifter_1_out), .\dist (subtractor_1_out), .out(shifter_3_out));
  Multiplexer #(.width(64)) multiplexer_1 (
    .in0(shifter_3_out), .in1(bit_extender_1_out), .out(multiplexer_1_out), .sel(comparator_1_eq));
  xor xor_1 (xor_1_out, b[0], 1'b0);
  Multiplexer #(.width(64)) multiplexer_2 (
    .in0(multiplexer_1_out), .in1(shifter_2_out), .out({multiplexer_2_out, res_low}), .sel(xor_1_out));
  assign res_high = {{31{a[31]}}, a[31]};  // Bit_Extender bit_extender_2

  assign done = 1'b1;
endmodule

module alu_circuit (
  input  [5:0] aluop,
  input  [31:0] a,
  input  [31:0] b,
  input  [4:0] Shamt,
  input  clk,
  input  rst,
  output [31:0] aluOut,
  output ZeroFlag,
  output NegativeFlag,
  output Done
);

  wire and_1_out, comparator_1_eq, DIV_done, isDiv;
  wire [5:0] Last_Aluop;
  wire [31:0] ADD_res_low, ANDD_res_low, bit_extender_1_out, DivHi, DivLo, Hi_q, Lo_q, MUL_res_low,
       multiplexer_1_out, multiplexer_2_out, ORR_res_low, Shamt_SLL_res_low, SLLL_res_low, SRAA_res_low,
       SRLL_res_low, SUB_res_low, XORR_res_low;

  assign bit_extender_1_out = {{27{1'b0}}, Shamt};  // Bit_Extender bit_extender_1
  Comparator #(.mode("unsigned"), .width(6)) comparator_1 (
    .a(Last_Aluop), .b(6'b011010), .eq(comparator_1_eq));  // open: gt, lt
  Comparator #(.mode("unsigned"), .width(6)) comparator_2 (.a(6'b011010), .b(aluop), .eq(isDiv));  // open: gt, lt
  and and_1 (and_1_out, ~comparator_1_eq, isDiv);  // AND_Gate
  Register #(.width(32)) Hi (.D(DivHi), .en(1'b1), .clk(clk), .Q(Hi_q), .clr(rst));
  Register #(.width(32)) Lo (.D(DivLo), .en(1'b1), .clk(clk), .Q(Lo_q), .clr(rst));
  add_circuit ADD (.a(a), .b(b), .res_low(ADD_res_low));  // open: done
  sub_circuit SUB (.a(a), .b(b), .res_low(SUB_res_low));  // open: res_high, done
  mul_circuit MUL (.multiplicand(a), .multiplierr(b), .res_low(MUL_res_low));
  div_circuit DIV (
    .start(and_1_out), .dividend(a), .divisor(b), .clk(clk), .remainder(DivHi), .quotient(DivLo),
    .done(DIV_done));
  and_circuit ANDD (.a(a), .b(b), .res_low(ANDD_res_low));  // open: res_high, done
  or_circuit ORR (.a(a), .b(b), .res_low(ORR_res_low));  // open: res_high, done
  xor_circuit XORR (.a(a), .b(b), .res_low(XORR_res_low));  // open: res_high, done
  sll_circuit SLLL (.a(a), .b(b), .res_low(SLLL_res_low));  // open: done
  sll_circuit Shamt_SLL (.a(b), .b(bit_extender_1_out), .res_low(Shamt_SLL_res_low));  // open: done
  srl_circuit SRLL (.a(a), .b(b), .res_low(SRLL_res_low));  // open: res_high, done
  sra_circuit SRAA (.a(a), .b(b), .res_low(SRAA_res_low));  // open: res_high, done
  Register #(.width(6)) u_Last_AluOp (.D(aluop), .en(1'b1), .clk(clk), .Q(Last_Aluop));  // open: clr
  Multiplexer #(.select(5), .width(32)) multiplexer_1 (
    .in0(Shamt_SLL_res_low), .in2(MUL_res_low), .in4(SLLL_res_low), .in6(SRLL_res_low), .in7(SRAA_res_low),
    .in16(Hi_q), .in18(Lo_q), .in26(DivLo), .out(multiplexer_1_out), .sel(aluop[4:0]));  // open: in1, in3, in5, in8, in9, in10, in11, in12, in13, in14, in15, in17, in19, in20, in21, in22, in23, in24, in25, in27, in28, in29, in30, in31
  Multiplexer #(.select(5), .width(32)) multiplexer_2 (
    .in0(ADD_res_low), .in2(SUB_res_low), .in4(ANDD_res_low), .in5(ORR_res_low), .in6(XORR_res_low),
    .out(multiplexer_2_out), .sel(aluop[4:0]));  // open: in1, in3, in7, in8, in9, in10, in11, in12, in13, in14, in15, in16, in17, in18, in19, in20, in21, in22, in23, in24, in25, in26, in27, in28, in29, in30, in31
  Multiplexer multiplexer_3 (.in0(1'b1), .in1(DIV_done), .out(Done), .sel(isDiv));
  Multiplexer #(.width(32)) multiplexer_4 (
    .in0(multiplexer_1_out), .in1(multiplexer_2_out), .out(aluOut), .sel(aluop[5]));
  Comparator #(.width(32)) comparator_3 (.a(aluOut), .b({32{1'b0}}), .eq(ZeroFlag), .lt(NegativeFlag));  // open: gt
endmodule

module control_circuit (
  input  [5:0] opcode,
  output RegDest,
  output ALUSrc,
  output [1:0] ALUOp,
  output [1:0] MemWrite,
  output MemToReg,
  output RegWrite,
  output isBranchN,
  output isJump,
  output isSLTI,
  output isBranch,
  output RegWrite_V,
  output RegDest_V,
  output is_TOCOP,
  output is_FROMCOP,
  output isVStore,
  output isRType
);

  wire Addi, comparator_1_eq, comparator_2_eq, Jump, JumpAndLink, Load, Load_v, Store;

  Comparator #(.width(6)) comparator_1 (.a(opcode), .b({6{1'b0}}), .eq(comparator_1_eq));  // open: gt, lt
  Comparator #(.width(6)) comparator_2 (.a(opcode), .b(6'b011100), .eq(comparator_2_eq));  // open: gt, lt
  Comparator #(.width(6)) comparator_3 (.a(opcode), .b(6'b000010), .eq(Jump));  // open: gt, lt
  Comparator #(.width(6)) comparator_4 (.a(opcode), .b(6'b000101), .eq(isBranchN));  // open: gt, lt
  Comparator #(.width(6)) comparator_5 (.a(opcode), .b(6'b000100), .eq(isBranch));  // open: gt, lt
  Comparator #(.width(6)) comparator_6 (.a(opcode), .b(6'b100011), .eq(Load));  // open: gt, lt
  Comparator #(.width(6)) comparator_7 (.a(opcode), .b(6'b101011), .eq(Store));  // open: gt, lt
  Comparator #(.width(6)) comparator_8 (.a(opcode), .b(6'b001010), .eq(isSLTI));  // open: gt, lt
  Comparator #(.width(6)) comparator_9 (.a(opcode), .b(6'b001000), .eq(Addi));  // open: gt, lt
  Comparator #(.width(6)) comparator_10 (.a(opcode), .b(6'b000011), .eq(JumpAndLink));  // open: gt, lt
  Comparator #(.width(6)) comparator_11 (.a(opcode), .b(6'b100100), .eq(Load_v));  // open: gt, lt
  Comparator #(.width(6)) comparator_12 (.a(opcode), .b(6'b101100), .eq(isVStore));  // open: gt, lt
  Comparator #(.width(6)) comparator_13 (.a(opcode), .b(6'b000111), .eq(is_FROMCOP));  // open: gt, lt
  Comparator #(.width(6)) comparator_14 (.a(opcode), .b(6'b000110), .eq(is_TOCOP));  // open: gt, lt
  Comparator #(.width(6)) comparator_15 (.a(opcode), .b(6'b000001), .eq(RegDest_V));  // open: gt, lt
  or or_1 (isRType, comparator_1_eq, comparator_2_eq);
  or or_2 (ALUOp[1], isBranch, isSLTI, isBranchN, isRType);
  or or_3 (MemWrite[0], Store, isVStore);
  or or_4 (MemWrite[1], isVStore, Load_v);
  or or_5 (ALUSrc, Load, Store, Addi, isSLTI, Load_v, isVStore);
  or or_6 (ALUOp[0], Load, Store, Addi, isRType, Load_v, isVStore);
  or or_7 (MemToReg, Load, Load_v);
  or or_8 (RegWrite, is_FROMCOP, isRType, Load, JumpAndLink, isSLTI, Addi);
  or or_9 (isJump, Jump, JumpAndLink);
  or or_10 (RegWrite_V, RegDest_V, Load_v, is_TOCOP);

  assign RegDest = isRType;

  // Other names for the same wires on the sheet: Branch = isBranch; BranchN = isBranchN; Fromcop = is_FROMCOP;
  //   RType = isRType; SetOnLessThan = isSLTI; Store_v = isVStore; Tocop = is_TOCOP; V_Type = RegDest_V
endmodule

module regfile_vector (
  input  clk,
  input  rst,
  input  [31:0] Dwrite0,
  input  [31:0] Dwrite1,
  input  [31:0] Dwrite2,
  input  [31:0] Dwrite3,
  input  is_tocop,
  input  [1:0] bit_tocop,
  input  [2:0] Awrite,
  input  [2:0] Aread0,
  input  [2:0] Aread1,
  output [31:0] Dread0_0,
  output [31:0] Dread0_1,
  output [31:0] Dread0_2,
  output [31:0] Dread0_3,
  output [31:0] Dread1_0,
  output [31:0] Dread1_1,
  output [31:0] Dread1_2,
  output [31:0] Dread1_3,
  output [31:0] R4,
  output [31:0] R5,
  output [31:0] R6,
  output [31:0] R7,
  output [31:0] R8,
  output [31:0] R9,
  output [31:0] R10,
  output [31:0] R11,
  output [31:0] R12,
  output [31:0] R13,
  output [31:0] R14,
  output [31:0] R15,
  output [31:0] R16,
  output [31:0] R17,
  output [31:0] R18,
  output [31:0] R19,
  output [31:0] R20,
  output [31:0] R21,
  output [31:0] R22,
  output [31:0] R23,
  output [31:0] R24,
  output [31:0] R25,
  output [31:0] R26,
  output [31:0] R27,
  output [31:0] R28,
  output [31:0] R29,
  output [31:0] R30,
  output [31:0] R31
);

  wire and_1_out, and_2_out, and_3_out, and_4_out, and_5_out, and_6_out, and_7_out, and_8_out, and_9_out,
       and_10_out, and_11_out, and_12_out, and_13_out, and_14_out, and_15_out, and_16_out, and_17_out,
       and_18_out, and_19_out, and_20_out, and_21_out, and_22_out, and_23_out, and_24_out, and_25_out,
       and_26_out, and_27_out, and_28_out, and_29_out, and_30_out, and_31_out, and_32_out, decoder_1_out0,
       decoder_1_out1, decoder_1_out2, decoder_1_out3, decoder_2_out0, decoder_2_out1, decoder_2_out2,
       decoder_2_out3, decoder_2_out4, decoder_2_out5, decoder_2_out6, decoder_2_out7, not_1_out, or_1_out,
       or_2_out, or_3_out, or_4_out, or_5_out, or_6_out, or_7_out, or_8_out, or_9_out, or_10_out, or_11_out,
       or_12_out, or_13_out, or_14_out, or_15_out, or_16_out, or_17_out, or_18_out, or_19_out, or_20_out,
       or_21_out, or_22_out, or_23_out, or_24_out, or_25_out, or_26_out, or_27_out, or_28_out, or_29_out,
       or_30_out, or_31_out, or_32_out, or_33_out, or_34_out, or_35_out, or_36_out, undriven_2, undriven_3,
       undriven_4, undriven_5;
  wire [31:0] multiplexer_1_out, multiplexer_2_out, multiplexer_3_out, multiplexer_4_out, register_2_q,
       register_10_q, register_18_q, undriven;

  Decoder #(.select(2)) decoder_1 (
    .out0(decoder_1_out0), .out1(decoder_1_out1), .out2(decoder_1_out2), .out3(decoder_1_out3),
    .sel(bit_tocop));  // open: en
  not not_1 (not_1_out, is_tocop);
  Register #(.width(32)) register_1 (.D(undriven), .en(or_1_out), .clk(undriven_2));  // open: Q, clr
  or or_1 (or_1_out, undriven_5, and_1_out);
  and and_1 (and_1_out, undriven_4, undriven_3);
  or or_2 (or_2_out, not_1_out, decoder_1_out0);
  or or_3 (or_3_out, not_1_out, decoder_1_out1);
  or or_4 (or_4_out, not_1_out, decoder_1_out2);
  or or_5 (or_5_out, not_1_out, decoder_1_out3);
  Decoder #(.select(3)) decoder_2 (
    .out0(decoder_2_out0), .out1(decoder_2_out1), .out2(decoder_2_out2), .out3(decoder_2_out3),
    .out4(decoder_2_out4), .out5(decoder_2_out5), .out6(decoder_2_out6), .out7(decoder_2_out7), .sel(Awrite));  // open: en
  Multiplexer #(.width(32)) multiplexer_1 (.in0(Dwrite0), .in1({32{1'b0}}), .out(multiplexer_1_out), .sel(rst));
  Multiplexer #(.width(32)) multiplexer_2 (.in0(Dwrite1), .in1({32{1'b0}}), .out(multiplexer_2_out), .sel(rst));
  Multiplexer #(.width(32)) multiplexer_3 (.in0(Dwrite2), .in1({32{1'b0}}), .out(multiplexer_3_out), .sel(rst));
  Multiplexer #(.width(32)) multiplexer_4 (.in0(Dwrite3), .in1({32{1'b0}}), .out(multiplexer_4_out), .sel(rst));
  and and_2 (and_2_out, or_2_out, decoder_2_out1);
  and and_3 (and_3_out, or_2_out, decoder_2_out2);
  and and_4 (and_4_out, or_2_out, decoder_2_out3);
  and and_5 (and_5_out, or_2_out, decoder_2_out4);
  and and_6 (and_6_out, or_2_out, decoder_2_out5);
  and and_7 (and_7_out, or_2_out, decoder_2_out6);
  and and_8 (and_8_out, or_2_out, decoder_2_out7);
  Register #(.width(32)) Reg4 (.D(multiplexer_1_out), .en(or_6_out), .clk(clk), .Q(R4));  // open: clr
  or or_6 (or_6_out, rst, and_2_out);
  Register #(.width(32)) Reg8 (.D(multiplexer_1_out), .en(or_7_out), .clk(clk), .Q(R8));  // open: clr
  or or_7 (or_7_out, rst, and_3_out);
  Register #(.width(32)) Reg12 (.D(multiplexer_1_out), .en(or_8_out), .clk(clk), .Q(R12));  // open: clr
  or or_8 (or_8_out, rst, and_4_out);
  Register #(.width(32)) Reg16 (.D(multiplexer_1_out), .en(or_9_out), .clk(clk), .Q(R16));  // open: clr
  or or_9 (or_9_out, rst, and_5_out);
  Register #(.width(32)) Reg20 (.D(multiplexer_1_out), .en(or_10_out), .clk(clk), .Q(R20));  // open: clr
  or or_10 (or_10_out, rst, and_6_out);
  Register #(.width(32)) Reg24 (.D(multiplexer_1_out), .en(or_11_out), .clk(clk), .Q(R24));  // open: clr
  or or_11 (or_11_out, rst, and_7_out);
  Register #(.width(32)) Reg28 (.D(multiplexer_1_out), .en(or_12_out), .clk(clk), .Q(R28));  // open: clr
  or or_12 (or_12_out, rst, and_8_out);
  Multiplexer #(.select(3), .width(32)) multiplexer_5 (
    .in0({32{1'b0}}), .in1(R4), .in2(R8), .in3(R12), .in4(R16), .in5(R20), .in6(R24), .in7(R28),
    .out(Dread0_0), .sel(Aread0));
  Multiplexer #(.select(3), .width(32)) multiplexer_6 (
    .in0({32{1'b0}}), .in1(R4), .in2(R8), .in3(R12), .in4(R16), .in5(R20), .in6(R24), .in7(R28),
    .out(Dread1_0), .sel(Aread1));
  and and_9 (and_9_out, or_3_out, decoder_2_out0);
  and and_10 (and_10_out, or_3_out, decoder_2_out1);
  and and_11 (and_11_out, or_3_out, decoder_2_out2);
  and and_12 (and_12_out, or_3_out, decoder_2_out3);
  and and_13 (and_13_out, or_3_out, decoder_2_out4);
  and and_14 (and_14_out, or_3_out, decoder_2_out5);
  and and_15 (and_15_out, or_3_out, decoder_2_out6);
  and and_16 (and_16_out, or_3_out, decoder_2_out7);
  Register #(.width(32)) register_2 (.D(multiplexer_2_out), .en(or_13_out), .clk(clk), .Q(register_2_q));  // open: clr
  or or_13 (or_13_out, rst, and_9_out);
  Register #(.width(32)) register_3 (.D(multiplexer_2_out), .en(or_14_out), .clk(clk), .Q(R5));  // open: clr
  or or_14 (or_14_out, rst, and_10_out);
  Register #(.width(32)) register_4 (.D(multiplexer_2_out), .en(or_15_out), .clk(clk), .Q(R9));  // open: clr
  or or_15 (or_15_out, rst, and_11_out);
  Register #(.width(32)) register_5 (.D(multiplexer_2_out), .en(or_16_out), .clk(clk), .Q(R13));  // open: clr
  or or_16 (or_16_out, rst, and_12_out);
  Register #(.width(32)) register_6 (.D(multiplexer_2_out), .en(or_17_out), .clk(clk), .Q(R17));  // open: clr
  or or_17 (or_17_out, rst, and_13_out);
  Register #(.width(32)) register_7 (.D(multiplexer_2_out), .en(or_18_out), .clk(clk), .Q(R21));  // open: clr
  or or_18 (or_18_out, rst, and_14_out);
  Register #(.width(32)) register_8 (.D(multiplexer_2_out), .en(or_19_out), .clk(clk), .Q(R25));  // open: clr
  or or_19 (or_19_out, rst, and_15_out);
  Register #(.width(32)) register_9 (.D(multiplexer_2_out), .en(or_20_out), .clk(clk), .Q(R29));  // open: clr
  or or_20 (or_20_out, rst, and_16_out);
  Multiplexer #(.select(3), .width(32)) multiplexer_7 (
    .in0({32{1'b0}}), .in1(R5), .in2(R9), .in3(R13), .in4(R17), .in5(R21), .in6(R25), .in7(R29),
    .out(Dread0_1), .sel(Aread0));
  Multiplexer #(.select(3), .width(32)) multiplexer_8 (
    .in0({32{1'b0}}), .in1(R5), .in2(R9), .in3(R13), .in4(R17), .in5(R21), .in6(R25), .in7(R29),
    .out(Dread1_1), .sel(Aread1));
  Register #(.width(32)) register_10 (
    .D(multiplexer_3_out), .en(or_21_out), .clk(clk), .Q(register_10_q));  // open: clr
  or or_21 (or_21_out, rst, and_17_out);
  and and_17 (and_17_out, or_4_out, decoder_2_out0);
  Register #(.width(32)) register_11 (.D(multiplexer_3_out), .en(or_22_out), .clk(clk), .Q(R6));  // open: clr
  or or_22 (or_22_out, rst, and_18_out);
  and and_18 (and_18_out, or_4_out, decoder_2_out1);
  Register #(.width(32)) register_12 (.D(multiplexer_3_out), .en(or_23_out), .clk(clk), .Q(R10));  // open: clr
  or or_23 (or_23_out, rst, and_19_out);
  and and_19 (and_19_out, or_4_out, decoder_2_out2);
  Register #(.width(32)) register_13 (.D(multiplexer_3_out), .en(or_24_out), .clk(clk), .Q(R14));  // open: clr
  or or_24 (or_24_out, rst, and_20_out);
  and and_20 (and_20_out, or_4_out, decoder_2_out3);
  Register #(.width(32)) register_14 (.D(multiplexer_3_out), .en(or_25_out), .clk(clk), .Q(R18));  // open: clr
  or or_25 (or_25_out, rst, and_21_out);
  and and_21 (and_21_out, or_4_out, decoder_2_out4);
  Register #(.width(32)) register_15 (.D(multiplexer_3_out), .en(or_26_out), .clk(clk), .Q(R22));  // open: clr
  or or_26 (or_26_out, rst, and_22_out);
  and and_22 (and_22_out, or_4_out, decoder_2_out5);
  Register #(.width(32)) register_16 (.D(multiplexer_3_out), .en(or_27_out), .clk(clk), .Q(R26));  // open: clr
  or or_27 (or_27_out, rst, and_23_out);
  and and_23 (and_23_out, or_4_out, decoder_2_out6);
  Register #(.width(32)) register_17 (.D(multiplexer_3_out), .en(or_28_out), .clk(clk), .Q(R30));  // open: clr
  or or_28 (or_28_out, rst, and_24_out);
  and and_24 (and_24_out, or_4_out, decoder_2_out7);
  Multiplexer #(.select(3), .width(32)) multiplexer_9 (
    .in0({32{1'b0}}), .in1(R6), .in2(R10), .in3(R14), .in4(R18), .in5(R22), .in6(R26), .in7(R30),
    .out(Dread0_2), .sel(Aread0));
  Multiplexer #(.select(3), .width(32)) multiplexer_10 (
    .in0({32{1'b0}}), .in1(R6), .in2(R10), .in3(R14), .in4(R18), .in5(R22), .in6(R26), .in7(R30),
    .out(Dread1_2), .sel(Aread1));
  Register #(.width(32)) register_18 (
    .D(multiplexer_4_out), .en(or_29_out), .clk(clk), .Q(register_18_q));  // open: clr
  or or_29 (or_29_out, rst, and_25_out);
  and and_25 (and_25_out, or_5_out, decoder_2_out0);
  Register #(.width(32)) register_19 (.D(multiplexer_4_out), .en(or_30_out), .clk(clk), .Q(R7));  // open: clr
  or or_30 (or_30_out, rst, and_26_out);
  and and_26 (and_26_out, or_5_out, decoder_2_out1);
  Register #(.width(32)) register_20 (.D(multiplexer_4_out), .en(or_31_out), .clk(clk), .Q(R11));  // open: clr
  or or_31 (or_31_out, rst, and_27_out);
  and and_27 (and_27_out, or_5_out, decoder_2_out2);
  Register #(.width(32)) register_21 (.D(multiplexer_4_out), .en(or_32_out), .clk(clk), .Q(R15));  // open: clr
  or or_32 (or_32_out, rst, and_28_out);
  and and_28 (and_28_out, or_5_out, decoder_2_out3);
  Register #(.width(32)) register_22 (.D(multiplexer_4_out), .en(or_33_out), .clk(clk), .Q(R19));  // open: clr
  or or_33 (or_33_out, rst, and_29_out);
  and and_29 (and_29_out, or_5_out, decoder_2_out4);
  Register #(.width(32)) register_23 (.D(multiplexer_4_out), .en(or_34_out), .clk(clk), .Q(R23));  // open: clr
  or or_34 (or_34_out, rst, and_30_out);
  and and_30 (and_30_out, or_5_out, decoder_2_out5);
  Register #(.width(32)) register_24 (.D(multiplexer_4_out), .en(or_35_out), .clk(clk), .Q(R27));  // open: clr
  or or_35 (or_35_out, rst, and_31_out);
  and and_31 (and_31_out, or_5_out, decoder_2_out6);
  Register #(.width(32)) register_25 (.D(multiplexer_4_out), .en(or_36_out), .clk(clk), .Q(R31));  // open: clr
  or or_36 (or_36_out, rst, and_32_out);
  and and_32 (and_32_out, or_5_out, decoder_2_out7);
  Multiplexer #(.select(3), .width(32)) multiplexer_11 (
    .in0({32{1'b0}}), .in1(R7), .in2(R11), .in3(R15), .in4(R19), .in5(R23), .in6(R27), .in7(R31),
    .out(Dread0_3), .sel(Aread0));
  Multiplexer #(.select(3), .width(32)) multiplexer_12 (
    .in0({32{1'b0}}), .in1(R7), .in2(R11), .in3(R15), .in4(R19), .in5(R23), .in6(R27), .in7(R31),
    .out(Dread1_3), .sel(Aread1));

  // Notes on the sheet:
  //   Field Template
endmodule

module alu_circuit128 (
  input  [5:0] aluop,
  input  [31:0] a0,
  input  [31:0] a1,
  input  [31:0] a2,
  input  [31:0] a3,
  input  [31:0] b0,
  input  [31:0] b1,
  input  [31:0] b2,
  input  [31:0] b3,
  output [31:0] aluOut_0,
  output [31:0] aluOut_1,
  output [31:0] aluOut_2,
  output [31:0] aluOut_3
);

  wire [31:0] not_1_out, not_2_out, not_3_out, not_4_out, V16_ADD_res_0, V16_ADD_res_1, V16_ADD_res_2,
       V16_ADD_res_3, V16_MUL_res_0, V16_MUL_res_1, V16_MUL_res_2, V16_MUL_res_3, V16_SUB_res_0,
       V16_SUB_res_1, V16_SUB_res_2, V16_SUB_res_3, V32_ADD_res_0, V32_ADD_res_1, V32_ADD_res_2,
       V32_ADD_res_3, V32_MUL_res_0, V32_MUL_res_1, V32_MUL_res_2, V32_MUL_res_3, V32_SUB_res_0,
       V32_SUB_res_1, V32_SUB_res_2, V32_SUB_res_3, VAND_res_0, VAND_res_1, VAND_res_2, VAND_res_3,
       VOR_res_0, VOR_res_1, VOR_res_2, VOR_res_3, VXOR_res_0, VXOR_res_1, VXOR_res_2, VXOR_res_3;

  assign not_1_out = ~a0;  // NOT_Gate not_1, 32 bits wide
  assign not_2_out = ~a1;  // NOT_Gate not_2, 32 bits wide
  assign not_3_out = ~a2;  // NOT_Gate not_3, 32 bits wide
  assign not_4_out = ~a3;  // NOT_Gate not_4, 32 bits wide
  mul_4x32_circuit V32_MUL (
    .multiplicand0(a0), .multiplierr0(b0), .multiplicand1(a1), .multiplierr1(b1), .multiplicand2(a2),
    .multiplierr2(b2), .multiplicand3(a3), .multiplierr3(b3), .res_0(V32_MUL_res_0), .res_1(V32_MUL_res_1),
    .res_2(V32_MUL_res_2), .res_3(V32_MUL_res_3));  // open: done
  add_4x32_circuit V32_ADD (
    .a0(a0), .b0(b0), .a1(a1), .b1(b1), .a2(a2), .b2(b2), .a3(a3), .b3(b3), .res_0(V32_ADD_res_0),
    .res_1(V32_ADD_res_1), .res_2(V32_ADD_res_2), .res_3(V32_ADD_res_3));  // open: done
  sub_4x32_circuit V32_SUB (
    .a0(a0), .b0(b0), .a1(a1), .b1(b1), .a2(a2), .b2(b2), .a3(a3), .b3(b3), .res_0(V32_SUB_res_0),
    .res_1(V32_SUB_res_1), .res_2(V32_SUB_res_2), .res_3(V32_SUB_res_3));  // open: done
  and_4x32_circuit VAND (
    .a0(a0), .b0(b0), .a1(a1), .b1(b1), .a2(a2), .b2(b2), .a3(a3), .b3(b3), .res_0(VAND_res_0),
    .res_1(VAND_res_1), .res_2(VAND_res_2), .res_3(VAND_res_3));  // open: done
  or_4x32_circuit VOR (
    .a0(a0), .b0(b0), .a1(a1), .b1(b1), .a2(a2), .b2(b2), .a3(a3), .b3(b3), .res_0(VOR_res_0),
    .res_1(VOR_res_1), .res_2(VOR_res_2), .res_3(VOR_res_3));  // open: done
  xor_4x32_circuit VXOR (
    .a0(a0), .b0(b0), .a1(a1), .b1(b1), .a2(a2), .b2(b2), .a3(a3), .b3(b3), .res_0(VXOR_res_0),
    .res_1(VXOR_res_1), .res_2(VXOR_res_2), .res_3(VXOR_res_3));  // open: done
  mul_8x16_circuit V16_MUL (
    .multiplicand0(a0[15:0]), .multiplierr0(b0[15:0]), .multiplicand1(a0[31:16]), .multiplierr1(b0[31:16]),
    .multiplicand2(a1[15:0]), .multiplierr2(b1[15:0]), .multiplicand3(a1[31:16]), .multiplierr3(b1[31:16]),
    .multiplicand4(a2[15:0]), .multiplierr4(b2[15:0]), .multiplicand5(a2[31:16]), .multiplierr5(b2[31:16]),
    .multiplicand6(a3[15:0]), .multiplierr6(b3[15:0]), .multiplicand7(a3[31:16]), .multiplierr7(b3[31:16]),
    .res_0(V16_MUL_res_0), .res_1(V16_MUL_res_1), .res_2(V16_MUL_res_2), .res_3(V16_MUL_res_3));  // open: done
  add_8x16_circuit V16_ADD (
    .a0(a0[15:0]), .b0(b0[15:0]), .a1(a0[31:16]), .b1(b0[31:16]), .a2(a1[15:0]), .b2(b1[15:0]),
    .a3(a1[31:16]), .b3(b1[31:16]), .a4(a2[15:0]), .b4(b2[15:0]), .a5(a2[31:16]), .b5(b2[31:16]),
    .a6(a3[15:0]), .b6(b3[15:0]), .a7(a3[31:16]), .b7(b3[31:16]), .res_0(V16_ADD_res_0),
    .res_1(V16_ADD_res_1), .res_2(V16_ADD_res_2), .res_3(V16_ADD_res_3));  // open: done
  sub_8x16_circuit V16_SUB (
    .a0(a0[15:0]), .b0(b0[15:0]), .a1(a0[31:16]), .b1(b0[31:16]), .a2(a1[15:0]), .b2(b1[15:0]),
    .a3(a1[31:16]), .b3(b1[31:16]), .a4(a2[15:0]), .b4(b2[15:0]), .a5(a2[31:16]), .b5(b2[31:16]),
    .a6(a3[15:0]), .b6(b3[15:0]), .a7(a3[31:16]), .b7(b3[31:16]), .res_0(V16_SUB_res_0),
    .res_1(V16_SUB_res_1), .res_2(V16_SUB_res_2), .res_3(V16_SUB_res_3));  // open: done
  Multiplexer #(.select(5), .width(32)) multiplexer_1 (
    .in0(V32_MUL_res_0), .in1(V32_ADD_res_0), .in2(V32_SUB_res_0), .in3(VAND_res_0), .in4(VOR_res_0),
    .in5(VXOR_res_0), .in6(not_1_out), .in7(V16_MUL_res_0), .in8(V16_ADD_res_0), .in9(V16_SUB_res_0),
    .out(aluOut_0), .sel(aluop[4:0]));  // open: in10, in11, in12, in13, in14, in15, in16, in17, in18, in19, in20, in21, in22, in23, in24, in25, in26, in27, in28, in29, in30, in31
  Multiplexer #(.select(5), .width(32)) multiplexer_2 (
    .in0(V32_MUL_res_1), .in1(V32_ADD_res_1), .in2(V32_SUB_res_1), .in3(VAND_res_1), .in4(VOR_res_1),
    .in5(VXOR_res_1), .in6(not_2_out), .in7(V16_MUL_res_1), .in8(V16_ADD_res_1), .in9(V16_SUB_res_1),
    .out(aluOut_1), .sel(aluop[4:0]));  // open: in10, in11, in12, in13, in14, in15, in16, in17, in18, in19, in20, in21, in22, in23, in24, in25, in26, in27, in28, in29, in30, in31
  Multiplexer #(.select(5), .width(32)) multiplexer_3 (
    .in0(V32_MUL_res_2), .in1(V32_ADD_res_2), .in2(V32_SUB_res_2), .in3(VAND_res_2), .in4(VOR_res_2),
    .in5(VXOR_res_2), .in6(not_3_out), .in7(V16_MUL_res_2), .in8(V16_ADD_res_2), .in9(V16_SUB_res_2),
    .out(aluOut_2), .sel(aluop[4:0]));  // open: in10, in11, in12, in13, in14, in15, in16, in17, in18, in19, in20, in21, in22, in23, in24, in25, in26, in27, in28, in29, in30, in31
  Multiplexer #(.select(5), .width(32)) multiplexer_4 (
    .in0(V32_MUL_res_3), .in1(V32_ADD_res_3), .in2(V32_SUB_res_3), .in3(VAND_res_3), .in4(VOR_res_3),
    .in5(VXOR_res_3), .in6(not_4_out), .in7(V16_MUL_res_3), .in8(V16_ADD_res_3), .in9(V16_SUB_res_3),
    .out(aluOut_3), .sel(aluop[4:0]));  // open: in10, in11, in12, in13, in14, in15, in16, in17, in18, in19, in20, in21, in22, in23, in24, in25, in26, in27, in28, in29, in30, in31
endmodule

module mul_8x16_circuit (
  input  [15:0] multiplicand0,
  input  [15:0] multiplierr0,
  input  [15:0] multiplicand1,
  input  [15:0] multiplierr1,
  input  [15:0] multiplicand2,
  input  [15:0] multiplierr2,
  input  [15:0] multiplicand3,
  input  [15:0] multiplierr3,
  input  [15:0] multiplicand4,
  input  [15:0] multiplierr4,
  input  [15:0] multiplicand5,
  input  [15:0] multiplierr5,
  input  [15:0] multiplicand6,
  input  [15:0] multiplierr6,
  input  [15:0] multiplicand7,
  input  [15:0] multiplierr7,
  output done,
  output [31:0] res_0,
  output [31:0] res_1,
  output [31:0] res_2,
  output [31:0] res_3
);

  Multiplier #(.mode("twosComplement"), .width(16)) multiplier_1 (
    .a(multiplicand0), .b(multiplierr0), .out(res_0[15:0]));  // open: cin, cout
  Multiplier #(.mode("twosComplement"), .width(16)) multiplier_2 (
    .a(multiplicand1), .b(multiplierr1), .out(res_0[31:16]));  // open: cin, cout
  Multiplier #(.mode("twosComplement"), .width(16)) multiplier_3 (
    .a(multiplicand2), .b(multiplierr2), .out(res_1[15:0]));  // open: cin, cout
  Multiplier #(.mode("twosComplement"), .width(16)) multiplier_4 (
    .a(multiplicand3), .b(multiplierr3), .out(res_1[31:16]));  // open: cin, cout
  Multiplier #(.mode("twosComplement"), .width(16)) multiplier_5 (
    .a(multiplicand4), .b(multiplierr4), .out(res_2[15:0]));  // open: cin, cout
  Multiplier #(.mode("twosComplement"), .width(16)) multiplier_6 (
    .a(multiplicand5), .b(multiplierr5), .out(res_2[31:16]));  // open: cin, cout
  Multiplier #(.mode("twosComplement"), .width(16)) multiplier_7 (
    .a(multiplicand6), .b(multiplierr6), .out(res_3[15:0]));  // open: cin, cout
  Multiplier #(.mode("twosComplement"), .width(16)) multiplier_8 (
    .a(multiplicand7), .b(multiplierr7), .out(res_3[31:16]));  // open: cin, cout

  assign done = 1'b1;
endmodule

module mul_4x32_circuit (
  input  [31:0] multiplicand0,
  input  [31:0] multiplierr0,
  input  [31:0] multiplicand1,
  input  [31:0] multiplierr1,
  input  [31:0] multiplicand2,
  input  [31:0] multiplierr2,
  input  [31:0] multiplicand3,
  input  [31:0] multiplierr3,
  output done,
  output [31:0] res_0,
  output [31:0] res_1,
  output [31:0] res_2,
  output [31:0] res_3
);

  Multiplier #(.mode("twosComplement"), .width(32)) multiplier_1 (
    .a(multiplicand0), .b(multiplierr0), .out(res_0));  // open: cin, cout
  Multiplier #(.mode("twosComplement"), .width(32)) multiplier_2 (
    .a(multiplicand1), .b(multiplierr1), .out(res_1));  // open: cin, cout
  Multiplier #(.mode("twosComplement"), .width(32)) multiplier_3 (
    .a(multiplicand2), .b(multiplierr2), .out(res_2));  // open: cin, cout
  Multiplier #(.mode("twosComplement"), .width(32)) multiplier_4 (
    .a(multiplicand3), .b(multiplierr3), .out(res_3));  // open: cin, cout

  assign done = 1'b1;
endmodule

module add_8x16_circuit (
  input  [15:0] a0,
  input  [15:0] b0,
  input  [15:0] a1,
  input  [15:0] b1,
  input  [15:0] a2,
  input  [15:0] b2,
  input  [15:0] a3,
  input  [15:0] b3,
  input  [15:0] a4,
  input  [15:0] b4,
  input  [15:0] a5,
  input  [15:0] b5,
  input  [15:0] a6,
  input  [15:0] b6,
  input  [15:0] a7,
  input  [15:0] b7,
  output done,
  output [31:0] res_0,
  output [31:0] res_1,
  output [31:0] res_2,
  output [31:0] res_3
);

  Adder #(.width(16)) adder_1 (.a(a0), .b(b0), .out(res_0[15:0]));  // open: cin, cout
  Adder #(.width(16)) adder_2 (.a(a1), .b(b1), .out(res_0[31:16]));  // open: cin, cout
  Adder #(.width(16)) adder_3 (.a(a2), .b(b2), .out(res_1[15:0]));  // open: cin, cout
  Adder #(.width(16)) adder_4 (.a(a3), .b(b3), .out(res_1[31:16]));  // open: cin, cout
  Adder #(.width(16)) adder_5 (.a(a4), .b(b4), .out(res_2[15:0]));  // open: cin, cout
  Adder #(.width(16)) adder_6 (.a(a5), .b(b5), .out(res_2[31:16]));  // open: cin, cout
  Adder #(.width(16)) adder_7 (.a(a6), .b(b6), .out(res_3[15:0]));  // open: cin, cout
  Adder #(.width(16)) adder_8 (.a(a7), .b(b7), .out(res_3[31:16]));  // open: cin, cout

  assign done = 1'b1;
endmodule

module add_4x32_circuit (
  input  [31:0] a0,
  input  [31:0] b0,
  input  [31:0] a1,
  input  [31:0] b1,
  input  [31:0] a2,
  input  [31:0] b2,
  input  [31:0] a3,
  input  [31:0] b3,
  output done,
  output [31:0] res_0,
  output [31:0] res_1,
  output [31:0] res_2,
  output [31:0] res_3
);

  Adder #(.width(32)) adder_1 (.a(a0), .b(b0), .out(res_0));  // open: cin, cout
  Adder #(.width(32)) adder_2 (.a(a1), .b(b1), .out(res_1));  // open: cin, cout
  Adder #(.width(32)) adder_3 (.a(a2), .b(b2), .out(res_2));  // open: cin, cout
  Adder #(.width(32)) adder_4 (.a(a3), .b(b3), .out(res_3));  // open: cin, cout

  assign done = 1'b1;
endmodule

module sub_8x16_circuit (
  input  [15:0] a0,
  input  [15:0] b0,
  input  [15:0] a1,
  input  [15:0] b1,
  input  [15:0] a2,
  input  [15:0] b2,
  input  [15:0] a3,
  input  [15:0] b3,
  input  [15:0] a4,
  input  [15:0] b4,
  input  [15:0] a5,
  input  [15:0] b5,
  input  [15:0] a6,
  input  [15:0] b6,
  input  [15:0] a7,
  input  [15:0] b7,
  output done,
  output [31:0] res_0,
  output [31:0] res_1,
  output [31:0] res_2,
  output [31:0] res_3
);

  Subtractor #(.width(16)) subtractor_1 (.a(a0), .b(b0), .out(res_0[15:0]));  // open: bin, bout
  Subtractor #(.width(16)) subtractor_2 (.a(a1), .b(b1), .out(res_0[31:16]));  // open: bin, bout
  Subtractor #(.width(16)) subtractor_3 (.a(a2), .b(b2), .out(res_1[15:0]));  // open: bin, bout
  Subtractor #(.width(16)) subtractor_4 (.a(a3), .b(b3), .out(res_1[31:16]));  // open: bin, bout
  Subtractor #(.width(16)) subtractor_5 (.a(a4), .b(b4), .out(res_2[15:0]));  // open: bin, bout
  Subtractor #(.width(16)) subtractor_6 (.a(a5), .b(b5), .out(res_2[31:16]));  // open: bin, bout
  Subtractor #(.width(16)) subtractor_7 (.a(a6), .b(b6), .out(res_3[15:0]));  // open: bin, bout
  Subtractor #(.width(16)) subtractor_8 (.a(a7), .b(b7), .out(res_3[31:16]));  // open: bin, bout

  assign done = 1'b1;
endmodule

module sub_4x32_circuit (
  input  [31:0] a0,
  input  [31:0] b0,
  input  [31:0] a1,
  input  [31:0] b1,
  input  [31:0] a2,
  input  [31:0] b2,
  input  [31:0] a3,
  input  [31:0] b3,
  output done,
  output [31:0] res_0,
  output [31:0] res_1,
  output [31:0] res_2,
  output [31:0] res_3
);

  Subtractor #(.width(32)) subtractor_1 (.a(a0), .b(b0), .out(res_0));  // open: bin, bout
  Subtractor #(.width(32)) subtractor_2 (.a(a1), .b(b1), .out(res_1));  // open: bin, bout
  Subtractor #(.width(32)) subtractor_3 (.a(a2), .b(b2), .out(res_2));  // open: bin, bout
  Subtractor #(.width(32)) subtractor_4 (.a(a3), .b(b3), .out(res_3));  // open: bin, bout

  assign done = 1'b1;
endmodule

module and_4x32_circuit (
  input  [31:0] a0,
  input  [31:0] b0,
  input  [31:0] a1,
  input  [31:0] b1,
  input  [31:0] a2,
  input  [31:0] b2,
  input  [31:0] a3,
  input  [31:0] b3,
  output done,
  output [31:0] res_0,
  output [31:0] res_1,
  output [31:0] res_2,
  output [31:0] res_3
);

  assign res_0 = a0 & b0;  // AND_Gate and_1, 32 bits wide
  assign res_1 = a1 & b1;  // AND_Gate and_2, 32 bits wide
  assign res_2 = a2 & b2;  // AND_Gate and_3, 32 bits wide
  assign res_3 = a3 & b3;  // AND_Gate and_4, 32 bits wide

  assign done = 1'b1;
endmodule

module or_4x32_circuit (
  input  [31:0] a0,
  input  [31:0] b0,
  input  [31:0] a1,
  input  [31:0] b1,
  input  [31:0] a2,
  input  [31:0] b2,
  input  [31:0] a3,
  input  [31:0] b3,
  output done,
  output [31:0] res_0,
  output [31:0] res_1,
  output [31:0] res_2,
  output [31:0] res_3
);

  assign res_0 = a0 | b0;  // OR_Gate or_1, 32 bits wide
  assign res_1 = a1 | b1;  // OR_Gate or_2, 32 bits wide
  assign res_2 = a2 | b2;  // OR_Gate or_3, 32 bits wide
  assign res_3 = a3 | b3;  // OR_Gate or_4, 32 bits wide

  assign done = 1'b1;
endmodule

module xor_4x32_circuit (
  input  [31:0] a0,
  input  [31:0] b0,
  input  [31:0] a1,
  input  [31:0] b1,
  input  [31:0] a2,
  input  [31:0] b2,
  input  [31:0] a3,
  input  [31:0] b3,
  output done,
  output [31:0] res_0,
  output [31:0] res_1,
  output [31:0] res_2,
  output [31:0] res_3
);

  assign res_0 = a0 ^ b0;  // XOR_Gate xor_1, 32 bits wide
  assign res_1 = a1 ^ b1;  // XOR_Gate xor_2, 32 bits wide
  assign res_2 = a2 ^ b2;  // XOR_Gate xor_3, 32 bits wide
  assign res_3 = a3 ^ b3;  // XOR_Gate xor_4, 32 bits wide

  assign done = 1'b1;
endmodule
